// Logisim project 实验1-ACM1801-U201814565-王家璇.circ as structural Verilog: 5 circuits, main circuit 一位二进制半加器
module \一位二进制半加器  (
  input  A,
  input  B,
  output S,
  output C
);

  xor xor_1 (S, A, B);
  and and_1 (C, A, B);

  // Notes on the sheet:
  //   S=A异或B
  //   C=A与B
endmodule

module \一位二进制全加器  (
  input  A,
  input  B,
  input  Ci,
  output S,
  output Co
);

  wire and_1_out, and_2_out, and_3_out, or_1_out, xor_1_out;

  and and_1 (and_1_out, A, B);
  and and_2 (and_2_out, B, Ci);
  and and_3 (and_3_out, A, Ci);
  xor xor_1 (xor_1_out, B, Ci);
  or or_1 (or_1_out, and_1_out, and_2_out);
  xor xor_2 (S, A, xor_1_out);
  or or_2 (Co, or_1_out, and_3_out);

  // Notes on the sheet:
  //   S=A异或（B异或C）
  //   Co=AB+BCi+ACi
endmodule

module \串行进位并行加法器  (
  input  A0,
  input  B0,
  input  C0,
  input  A1,
  input  B1,
  input  A2,
  input  B2,
  input  A3,
  input  B3,
  output S0,
  output S1,
  output S2,
  output S3,
  output C4
);

  wire \一位二进制全加器_1_co , \一位二进制全加器_2_co , \一位二进制全加器_3_co ;

  \一位二进制全加器  \u_一位二进制全加器_1  (.A(A0), .B(B0), .Ci(C0), .S(S0), .Co(\一位二进制全加器_1_co ));
  \一位二进制全加器  \u_一位二进制全加器_2  (.A(A1), .B(B1), .Ci(\一位二进制全加器_1_co ), .S(S1), .Co(\一位二进制全加器_2_co ));
  \一位二进制全加器  \u_一位二进制全加器_3  (.A(A2), .B(B2), .Ci(\一位二进制全加器_2_co ), .S(S2), .Co(\一位二进制全加器_3_co ));
  \一位二进制全加器  \u_一位二进制全加器_4  (.A(A3), .B(B3), .Ci(\一位二进制全加器_3_co ), .S(S3), .Co(C4));
endmodule

module \先行进位并行加法器  (
  input  A0,
  input  B0,
  input  C0,
  input  A1,
  input  B1,
  input  A2,
  input  B2,
  input  A3,
  input  B3,
  output S0,
  output S1,
  output S2,
  output S3,
  output C4
);

  wire and_1_out, and_2_out, and_3_out, and_4_out, and_5_out, and_6_out, and_7_out, and_8_out, and_9_out,
       and_10_out, and_11_out, and_12_out, and_13_out, and_14_out, and_15_out, and_16_out, and_17_out,
       and_18_out, and_19_out, and_20_out, and_21_out, and_22_out, and_23_out, and_24_out, or_1_out,
       or_2_out, or_3_out, or_4_out, or_5_out, or_6_out, or_7_out, or_8_out, or_9_out, xor_1_out, xor_2_out,
       xor_3_out, xor_4_out;

  and and_1 (and_1_out, A0, B0);
  xor xor_1 (xor_1_out, A0, B0);
  and and_2 (and_2_out, A1, B1);
  xor xor_2 (xor_2_out, A1, B1);
  and and_3 (and_3_out, A2, B2);
  xor xor_3 (xor_3_out, A2, B2);
  and and_4 (and_4_out, A3, B3);
  xor xor_4 (xor_4_out, A3, B3);
  and and_5 (and_5_out, and_3_out, xor_4_out);
  and and_6 (and_6_out, xor_3_out, xor_4_out);
  and and_7 (and_7_out, xor_1_out, C0);
  and and_8 (and_8_out, xor_2_out, xor_3_out);
  and and_9 (and_9_out, and_2_out, xor_3_out);
  and and_10 (and_10_out, xor_1_out, xor_2_out);
  and and_11 (and_11_out, xor_3_out, xor_4_out);
  and and_12 (and_12_out, and_1_out, xor_2_out);
  and and_13 (and_13_out, xor_3_out, xor_4_out);
  and and_14 (and_14_out, and_2_out, and_6_out);
  or or_1 (or_1_out, and_5_out, and_4_out);
  or or_2 (or_2_out, and_7_out, and_1_out);
  and and_15 (and_15_out, xor_1_out, C0);
  and and_16 (and_16_out, and_1_out, xor_2_out);
  and and_17 (and_17_out, C0, xor_1_out);
  and and_18 (and_18_out, xor_2_out, xor_3_out);
  and and_19 (and_19_out, and_1_out, and_8_out);
  and and_20 (and_20_out, and_10_out, and_11_out);
  and and_21 (and_21_out, and_12_out, and_13_out);
  and and_22 (and_22_out, and_15_out, xor_2_out);
  or or_3 (or_3_out, and_16_out, and_2_out);
  and and_23 (and_23_out, C0, and_20_out);
  or or_4 (or_4_out, and_22_out, or_3_out);
  and and_24 (and_24_out, and_17_out, and_18_out);
  or or_5 (or_5_out, and_23_out, and_21_out);
  or or_6 (or_6_out, and_14_out, or_1_out);
  or or_7 (or_7_out, and_24_out, and_19_out);
  or or_8 (or_8_out, and_9_out, and_3_out);
  or or_9 (or_9_out, or_7_out, or_8_out);
  or or_10 (C4, or_5_out, or_6_out);
  xor xor_5 (S0, xor_1_out, C0);
  xor xor_6 (S1, or_2_out, xor_2_out);
  xor xor_7 (S2, or_4_out, xor_3_out);
  xor xor_8 (S3, xor_4_out, or_9_out);
endmodule

module \先行进位并行加法器测试电路  (
  input  in_1,
  input  in_2,
  input  in_3,
  input  in_4,
  input  in_5,
  input  in_6,
  input  in_7,
  input  in_8,
  input  in_9,
  output out_10,
  output out_11,
  output out_12,
  output out_13,
  output out_14
);

  \先行进位并行加法器  \u_先行进位并行加法器_1  (
    .A0(in_5), .B0(in_9), .C0(in_1), .A1(in_4), .B1(in_8), .A2(in_3), .B2(in_7), .A3(in_2), .B3(in_6),
    .S0(out_13), .S1(out_12), .S2(out_11), .S3(out_10), .C4(out_14));
endmodule
