// Logisim project 实验2-ACM1801-U201814565-王家璇.circ as structural Verilog: 10 circuits, main circuit 四位二进制可逆计数器
module \四位二进制可逆计数器  (
  input  D,
  input  C,
  input  B,
  input  A,
  input  \LD拔 ,
  input  CPu,
  input  CPd,
  input  CLR,
  output out_9,
  output out_10,
  output out_11,
  output out_12
);

  wire and_1_out, and_2_out, and_3_out, and_4_out, and_5_out, and_6_out, and_7_out, and_8_out, and_9_out,
       and_10_out, and_11_out, and_12_out, and_13_out, and_14_out, and_15_out, and_16_out, and_17_out,
       and_18_out, and_19_out, and_20_out, and_21_out, and_22_out, d_ff_1_qn, d_ff_2_qn, d_ff_3_qn,
       d_ff_4_qn, not_1_out, not_2_out, not_3_out, not_4_out, not_5_out, or_1_out, or_2_out, or_3_out,
       or_4_out, or_5_out, or_6_out, or_7_out, or_8_out;

  not not_1 (not_1_out, D);
  not not_2 (not_2_out, C);
  not not_3 (not_3_out, B);
  not not_4 (not_4_out, A);
  not not_5 (not_5_out, \LD拔 );
  and and_1 (and_1_out, D, not_5_out);
  and and_2 (and_2_out, not_1_out, not_5_out);
  and and_3 (and_3_out, C, not_5_out);
  and and_4 (and_4_out, not_2_out, not_5_out);
  and and_5 (and_5_out, B, not_5_out);
  and and_6 (and_6_out, not_3_out, not_5_out);
  and and_7 (and_7_out, A, not_5_out);
  and and_8 (and_8_out, not_4_out, not_5_out);
  and and_9 (and_9_out, out_11, out_10);
  and and_10 (and_10_out, d_ff_3_qn, d_ff_2_qn);
  and and_11 (and_11_out, CPu, and_12_out);
  and and_12 (and_12_out, out_12, and_9_out);
  and and_13 (and_13_out, CPd, and_14_out);
  and and_14 (and_14_out, d_ff_4_qn, and_10_out);
  and and_15 (and_15_out, CPu, and_16_out);
  and and_16 (and_16_out, out_11, out_12);
  and and_17 (and_17_out, CPd, and_18_out);
  and and_18 (and_18_out, d_ff_3_qn, d_ff_4_qn);
  and and_19 (and_19_out, out_12, CPu);
  and and_20 (and_20_out, d_ff_4_qn, CPd);
  and and_21 (and_21_out, CPu, 1'b1);
  and and_22 (and_22_out, CPd, 1'b1);
  or or_1 (or_1_out, and_11_out, and_13_out);
  or or_2 (or_2_out, and_15_out, and_17_out);
  or or_3 (or_3_out, and_19_out, and_20_out);
  or or_4 (or_4_out, and_21_out, and_22_out);
  D_Flip_Flop #(.trigger("falling"), .Pre_Clr_Positions("ABOVE_BELOW"), .NegatePresetClear("false"), .enable("false"), .NewFFLayout("true")) d_ff_1 (
    .clk(or_1_out), .D(d_ff_1_qn), .Q(out_9), .Qn(d_ff_1_qn), .preset(and_1_out), .reset(or_5_out));
  or or_5 (or_5_out, and_2_out, CLR);
  D_Flip_Flop #(.trigger("falling"), .Pre_Clr_Positions("ABOVE_BELOW"), .NegatePresetClear("false"), .enable("false"), .NewFFLayout("true")) d_ff_2 (
    .clk(or_2_out), .D(d_ff_2_qn), .Q(out_10), .Qn(d_ff_2_qn), .preset(and_3_out), .reset(or_6_out));
  or or_6 (or_6_out, CLR, and_4_out);
  D_Flip_Flop #(.trigger("falling"), .Pre_Clr_Positions("ABOVE_BELOW"), .NegatePresetClear("false"), .enable("false"), .NewFFLayout("true")) d_ff_3 (
    .clk(or_3_out), .D(d_ff_3_qn), .Q(out_11), .Qn(d_ff_3_qn), .preset(and_5_out), .reset(or_7_out));
  or or_7 (or_7_out, and_6_out, CLR);
  D_Flip_Flop #(.trigger("falling"), .Pre_Clr_Positions("ABOVE_BELOW"), .NegatePresetClear("false"), .enable("false"), .NewFFLayout("true")) d_ff_4 (
    .clk(or_4_out), .D(d_ff_4_qn), .Q(out_12), .Qn(d_ff_4_qn), .preset(and_7_out), .reset(or_8_out));
  or or_8 (or_8_out, CLR, and_8_out);
endmodule

module \四位二进制可逆计数器测试电路  (
  input  in_1,
  input  in_2,
  input  in_3,
  input  in_4,
  input  in_5,
  input  in_6,
  output out_7,
  output out_8,
  output out_9,
  output out_10
);

  wire button_1_out, button_2_out;

  Button button_1 (.out(button_1_out));
  Button button_2 (.out(button_2_out));
  \四位二进制可逆计数器  \u_四位二进制可逆计数器_1  (
    .D(in_2), .C(in_3), .B(in_4), .A(in_5), .out_9(out_7), .out_10(out_8), .out_11(out_9), .out_12(out_10),
    .\LD拔 (in_6), .CLR(in_1), .CPu(button_1_out), .CPd(button_2_out));
endmodule

module \二进制转8421码电路  (
  input  in_1,
  input  in_2,
  input  in_3,
  input  in_4,
  output out_5,
  output out_6,
  output out_7,
  output out_8,
  output out_9,
  output out_10,
  output out_11,
  output out_12
);

  wire or_1_out;

  and and_1 (out_8, in_1, or_1_out);
  or or_1 (or_1_out, in_2, in_3);
  \先行进位并行加法器  \u_先行进位并行加法器_1  (
    .A0(in_4), .B0(1'b0), .C0(1'b0), .A1(in_3), .B1(out_8), .A2(in_2), .B2(out_8), .A3(in_1), .B3(1'b0),
    .S0(out_12), .S1(out_11), .S2(out_10), .S3(out_9));  // open: C4

  assign out_5 = 1'b0;
  assign out_6 = 1'b0;
  assign out_7 = 1'b0;
endmodule

module \二进制转8421码测试电路  (
  input  in_1,
  input  in_2,
  input  in_3,
  input  in_4,
  input  in_5,
  input  in_6,
  input  in_7,
  input  in_8,
  input  in_9,
  input  in_10,
  output out_11,
  output out_12,
  output out_13,
  output out_14,
  output out_15,
  output out_16,
  output out_17,
  output out_18,
  output out_19,
  output out_20,
  output out_21,
  output out_22,
  output out_23,
  output out_24,
  output out_25,
  output out_26
);

  wire button_1_out, button_2_out, \四位二进制可逆计数器_1_out_9 , \四位二进制可逆计数器_1_out_10 , \四位二进制可逆计数器_1_out_11 ,
       \四位二进制可逆计数器_1_out_12 ;

  \二进制转8421码电路  \u_二进制转8421码电路_1  (
    .out_5(out_11), .out_6(out_12), .out_7(out_13), .out_8(out_14), .out_9(out_15), .out_10(out_16),
    .out_11(out_17), .out_12(out_18), .in_1(in_1), .in_2(in_2), .in_3(in_3), .in_4(in_4));
  Button button_1 (.out(button_1_out));
  Button button_2 (.out(button_2_out));
  \二进制转8421码电路  \u_二进制转8421码电路_2  (
    .out_5(out_19), .out_6(out_20), .out_7(out_21), .out_8(out_22), .out_9(out_23), .out_10(out_24),
    .out_11(out_25), .out_12(out_26), .in_1(\四位二进制可逆计数器_1_out_9 ), .in_2(\四位二进制可逆计数器_1_out_10 ),
    .in_3(\四位二进制可逆计数器_1_out_11 ), .in_4(\四位二进制可逆计数器_1_out_12 ));
  \四位二进制可逆计数器  \u_四位二进制可逆计数器_1  (
    .D(in_6), .C(in_7), .B(in_8), .A(in_9), .out_9(\四位二进制可逆计数器_1_out_9 ), .out_10(\四位二进制可逆计数器_1_out_10 ),
    .out_11(\四位二进制可逆计数器_1_out_11 ), .out_12(\四位二进制可逆计数器_1_out_12 ), .\LD拔 (in_10), .CLR(in_5),
    .CPu(button_1_out), .CPd(button_2_out));

  // Notes on the sheet:
  //   测试电路1
  //   测试电路2
endmodule

module \显示电路  (
  input  A3,
  input  A2,
  input  A1,
  input  A0,
  output g,
  output a,
  output f,
  output c,
  output b,
  output d,
  output e
);

  wire and_1_out, and_2_out, and_3_out, and_4_out, and_5_out, and_6_out, and_7_out, and_8_out, and_9_out,
       and_10_out, and_11_out, and_12_out, and_13_out, and_14_out, and_15_out, and_16_out, and_17_out,
       and_18_out, and_19_out, not_1_out, not_2_out, not_3_out, not_4_out, or_1_out, or_2_out, or_3_out,
       or_4_out, or_5_out, or_6_out, or_7_out, or_9_out, or_10_out, or_12_out;

  not not_1 (not_1_out, A3);
  not not_2 (not_2_out, A2);
  not not_3 (not_3_out, A1);
  not not_4 (not_4_out, A0);
  and and_1 (and_1_out, A1, A0);
  and and_2 (and_2_out, not_1_out, A1);
  and and_3 (and_3_out, A3, not_3_out);
  and and_4 (and_4_out, A3, not_2_out);
  and and_5 (and_5_out, not_1_out, A2);
  and and_6 (and_6_out, not_1_out, not_2_out);
  and and_7 (and_7_out, not_2_out, not_3_out);
  and and_8 (and_8_out, A2, not_3_out);
  and and_9 (and_9_out, A2, not_3_out);
  and and_10 (and_10_out, not_2_out, A1);
  and and_11 (and_11_out, not_1_out, and_1_out);
  and and_12 (and_12_out, not_3_out, not_4_out);
  and and_13 (and_13_out, A2, not_4_out);
  and and_14 (and_14_out, not_2_out, not_4_out);
  and and_15 (and_15_out, A1, not_4_out);
  or or_1 (or_1_out, and_3_out, and_5_out);
  or or_2 (or_2_out, and_3_out, and_9_out);
  or or_3 (or_3_out, and_2_out, and_12_out);
  or or_4 (or_4_out, and_6_out, and_12_out);
  or or_5 (or_5_out, and_7_out, and_11_out);
  or or_6 (or_6_out, and_8_out, and_15_out);
  or or_7 (or_7_out, and_12_out, and_13_out);
  or or_8 (e, and_14_out, and_15_out);
  or or_9 (or_9_out, and_4_out, and_10_out);
  and and_16 (and_16_out, or_1_out, A0);
  and and_17 (and_17_out, not_2_out, or_3_out);
  or or_10 (or_10_out, and_5_out, and_7_out);
  and and_18 (and_18_out, not_2_out, A0);
  or or_11 (b, or_4_out, or_5_out);
  or or_12 (or_12_out, and_10_out, e);
  or or_13 (g, or_9_out, or_6_out);
  or or_14 (a, and_16_out, and_17_out);
  or or_15 (c, or_10_out, and_18_out);
  and and_19 (and_19_out, and_9_out, A0);
  or or_16 (f, or_2_out, or_7_out);
  or or_17 (d, and_19_out, or_12_out);
endmodule

module \显示电路测试电路  (
  input  in_1,
  input  in_2,
  input  in_3,
  input  in_4
);

  wire \显示电路_1_a , \显示电路_1_b , \显示电路_1_c , \显示电路_1_d , \显示电路_1_e , \显示电路_1_f , \显示电路_1_g ;

  _7_Segment_Display #(.active("true")) u_7_segment_display_1 (
    .g(\显示电路_1_g ), .f(\显示电路_1_f ), .a(\显示电路_1_a ), .b(\显示电路_1_b ), .e(\显示电路_1_e ), .d(\显示电路_1_d ),
    .c(\显示电路_1_c ));  // open: dp
  \显示电路  \u_显示电路_1  (
    .A3(in_1), .A2(in_2), .A1(in_3), .A0(in_4), .a(\显示电路_1_a ), .f(\显示电路_1_f ), .b(\显示电路_1_b ),
    .c(\显示电路_1_c ), .g(\显示电路_1_g ), .d(\显示电路_1_d ), .e(\显示电路_1_e ));
endmodule

module \报警电路  (
  input  A,
  input  B,
  input  C,
  input  D,
  input  in,
  input  in2,
  output out1,
  output out3,
  output out2
);

  wire and_1_out, and_2_out, and_3_out, and_5_out, and_6_out, and_7_out, not_1_out, not_2_out, not_3_out,
       not_4_out, not_5_out, not_6_out;

  and and_1 (and_1_out, A, B);
  and and_2 (and_2_out, C, D);
  not not_1 (not_1_out, and_3_out);
  and and_3 (and_3_out, and_1_out, and_2_out);
  not not_2 (not_2_out, A);
  not not_3 (not_3_out, B);
  not not_4 (not_4_out, C);
  not not_5 (not_5_out, D);
  and and_4 (out1, not_1_out, in);
  and and_5 (and_5_out, not_2_out, not_3_out);
  and and_6 (and_6_out, and_5_out, and_7_out);
  and and_7 (and_7_out, not_4_out, not_5_out);
  not not_6 (not_6_out, and_6_out);
  and and_8 (out3, and_3_out, in);
  and and_9 (out2, not_6_out, in2);
endmodule

module \小型实验室门禁系统  (
  input  in_1,
  input  in_2,
  input  in_3,
  output out_4,
  output out_5,
  output out_6,
  output out_7,
  output out_8,
  output out_9,
  output out_10,
  output out_11,
  output out_12,
  output out_13,
  output out_14,
  output out_15,
  output out_16,
  output out_17,
  output out_18
);

  wire \二进制转8421码电路_1_out_5 , \二进制转8421码电路_1_out_6 , \二进制转8421码电路_1_out_7 , \二进制转8421码电路_1_out_8 ,
       \二进制转8421码电路_1_out_9 , \二进制转8421码电路_1_out_10 , \二进制转8421码电路_1_out_11 , \二进制转8421码电路_1_out_12 ,
       \四位二进制可逆计数器_1_out_9 , \四位二进制可逆计数器_1_out_10 , \四位二进制可逆计数器_1_out_11 , \四位二进制可逆计数器_1_out_12 ,
       \报警电路_1_out1 , \报警电路_1_out2 ;

  \报警电路  \u_报警电路_1  (
    .A(\四位二进制可逆计数器_1_out_9 ), .B(\四位二进制可逆计数器_1_out_10 ), .C(\四位二进制可逆计数器_1_out_11 ),
    .D(\四位二进制可逆计数器_1_out_12 ), .in(in_1), .in2(in_3), .out1(\报警电路_1_out1 ), .out2(\报警电路_1_out2 ),
    .out3(out_18));
  \显示电路  \u_显示电路_1  (
    .A3(\二进制转8421码电路_1_out_5 ), .A2(\二进制转8421码电路_1_out_6 ), .A1(\二进制转8421码电路_1_out_7 ),
    .A0(\二进制转8421码电路_1_out_8 ), .a(out_4), .f(out_9), .b(out_5), .c(out_6), .g(out_10), .d(out_7), .e(out_8));
  \二进制转8421码电路  \u_二进制转8421码电路_1  (
    .out_5(\二进制转8421码电路_1_out_5 ), .out_6(\二进制转8421码电路_1_out_6 ), .out_7(\二进制转8421码电路_1_out_7 ),
    .out_8(\二进制转8421码电路_1_out_8 ), .out_9(\二进制转8421码电路_1_out_9 ), .out_10(\二进制转8421码电路_1_out_10 ),
    .out_11(\二进制转8421码电路_1_out_11 ), .out_12(\二进制转8421码电路_1_out_12 ), .in_1(\四位二进制可逆计数器_1_out_9 ),
    .in_2(\四位二进制可逆计数器_1_out_10 ), .in_3(\四位二进制可逆计数器_1_out_11 ), .in_4(\四位二进制可逆计数器_1_out_12 ));
  \四位二进制可逆计数器  \u_四位二进制可逆计数器_1  (
    .D(1'b0), .C(1'b0), .B(1'b0), .A(1'b0), .out_9(\四位二进制可逆计数器_1_out_9 ), .out_10(\四位二进制可逆计数器_1_out_10 ),
    .out_11(\四位二进制可逆计数器_1_out_11 ), .out_12(\四位二进制可逆计数器_1_out_12 ), .\LD拔 (1'b1), .CLR(in_2),
    .CPu(\报警电路_1_out1 ), .CPd(\报警电路_1_out2 ));
  \显示电路  \u_显示电路_2  (
    .A3(\二进制转8421码电路_1_out_9 ), .A2(\二进制转8421码电路_1_out_10 ), .A1(\二进制转8421码电路_1_out_11 ),
    .A0(\二进制转8421码电路_1_out_12 ), .a(out_11), .f(out_16), .b(out_12), .c(out_13), .g(out_17), .d(out_14),
    .e(out_15));
endmodule

module \小型门禁系统测试电路  (
  input  in_1
);

  wire button_1_out, button_2_out, \小型实验室门禁系统_1_out_4 , \小型实验室门禁系统_1_out_5 , \小型实验室门禁系统_1_out_6 ,
       \小型实验室门禁系统_1_out_7 , \小型实验室门禁系统_1_out_8 , \小型实验室门禁系统_1_out_9 , \小型实验室门禁系统_1_out_10 ,
       \小型实验室门禁系统_1_out_11 , \小型实验室门禁系统_1_out_12 , \小型实验室门禁系统_1_out_13 , \小型实验室门禁系统_1_out_14 ,
       \小型实验室门禁系统_1_out_15 , \小型实验室门禁系统_1_out_16 , \小型实验室门禁系统_1_out_17 , \小型实验室门禁系统_1_out_18 ;

  Button button_1 (.out(button_1_out));
  Button button_2 (.out(button_2_out));
  \小型实验室门禁系统  \u_小型实验室门禁系统_1  (
    .in_1(button_1_out), .in_2(in_1), .in_3(button_2_out), .out_18(\小型实验室门禁系统_1_out_18 ),
    .out_4(\小型实验室门禁系统_1_out_4 ), .out_5(\小型实验室门禁系统_1_out_5 ), .out_6(\小型实验室门禁系统_1_out_6 ),
    .out_7(\小型实验室门禁系统_1_out_7 ), .out_8(\小型实验室门禁系统_1_out_8 ), .out_9(\小型实验室门禁系统_1_out_9 ),
    .out_10(\小型实验室门禁系统_1_out_10 ), .out_11(\小型实验室门禁系统_1_out_11 ), .out_12(\小型实验室门禁系统_1_out_12 ),
    .out_13(\小型实验室门禁系统_1_out_13 ), .out_14(\小型实验室门禁系统_1_out_14 ), .out_15(\小型实验室门禁系统_1_out_15 ),
    .out_16(\小型实验室门禁系统_1_out_16 ), .out_17(\小型实验室门禁系统_1_out_17 ));
  _7_Segment_Display #(.active("true")) u_7_segment_display_1 (
    .g(\小型实验室门禁系统_1_out_10 ), .f(\小型实验室门禁系统_1_out_9 ), .a(\小型实验室门禁系统_1_out_4 ), .b(\小型实验室门禁系统_1_out_5 ),
    .e(\小型实验室门禁系统_1_out_8 ), .d(\小型实验室门禁系统_1_out_7 ), .c(\小型实验室门禁系统_1_out_6 ));  // open: dp
  _7_Segment_Display #(.active("true")) u_7_segment_display_2 (
    .g(\小型实验室门禁系统_1_out_17 ), .f(\小型实验室门禁系统_1_out_16 ), .a(\小型实验室门禁系统_1_out_11 ), .b(\小型实验室门禁系统_1_out_12 ),
    .e(\小型实验室门禁系统_1_out_15 ), .d(\小型实验室门禁系统_1_out_14 ), .c(\小型实验室门禁系统_1_out_13 ));  // open: dp
  LED #(.active("true")) led_1 (.in(\小型实验室门禁系统_1_out_18 ));

  // Notes on the sheet:
  //   十位
  //   个位
endmodule

module \先行进位并行加法器  (
  input  A0,
  input  B0,
  input  C0,
  input  A1,
  input  B1,
  input  A2,
  input  B2,
  input  A3,
  input  B3,
  output S0,
  output S1,
  output S2,
  output S3,
  output C4
);

  wire and_1_out, and_2_out, and_3_out, and_4_out, and_5_out, and_6_out, and_7_out, and_8_out, and_9_out,
       and_10_out, and_11_out, and_12_out, and_13_out, and_14_out, and_15_out, and_16_out, and_17_out,
       and_18_out, and_19_out, and_20_out, and_21_out, and_22_out, and_23_out, and_24_out, or_1_out,
       or_2_out, or_3_out, or_4_out, or_5_out, or_6_out, or_7_out, or_8_out, or_9_out, xor_1_out, xor_2_out,
       xor_3_out, xor_4_out;

  and and_1 (and_1_out, A0, B0);
  xor xor_1 (xor_1_out, A0, B0);
  and and_2 (and_2_out, A1, B1);
  xor xor_2 (xor_2_out, A1, B1);
  and and_3 (and_3_out, A2, B2);
  xor xor_3 (xor_3_out, A2, B2);
  and and_4 (and_4_out, A3, B3);
  xor xor_4 (xor_4_out, A3, B3);
  and and_5 (and_5_out, and_3_out, xor_4_out);
  and and_6 (and_6_out, xor_3_out, xor_4_out);
  and and_7 (and_7_out, xor_1_out, C0);
  and and_8 (and_8_out, xor_2_out, xor_3_out);
  and and_9 (and_9_out, and_2_out, xor_3_out);
  and and_10 (and_10_out, xor_1_out, xor_2_out);
  and and_11 (and_11_out, xor_3_out, xor_4_out);
  and and_12 (and_12_out, and_1_out, xor_2_out);
  and and_13 (and_13_out, xor_3_out, xor_4_out);
  and and_14 (and_14_out, and_2_out, and_6_out);
  or or_1 (or_1_out, and_5_out, and_4_out);
  or or_2 (or_2_out, and_7_out, and_1_out);
  and and_15 (and_15_out, xor_1_out, C0);
  and and_16 (and_16_out, and_1_out, xor_2_out);
  and and_17 (and_17_out, C0, xor_1_out);
  and and_18 (and_18_out, xor_2_out, xor_3_out);
  and and_19 (and_19_out, and_1_out, and_8_out);
  and and_20 (and_20_out, and_10_out, and_11_out);
  and and_21 (and_21_out, and_12_out, and_13_out);
  and and_22 (and_22_out, and_15_out, xor_2_out);
  or or_3 (or_3_out, and_16_out, and_2_out);
  and and_23 (and_23_out, C0, and_20_out);
  or or_4 (or_4_out, and_22_out, or_3_out);
  and and_24 (and_24_out, and_17_out, and_18_out);
  or or_5 (or_5_out, and_23_out, and_21_out);
  or or_6 (or_6_out, and_14_out, or_1_out);
  or or_7 (or_7_out, and_24_out, and_19_out);
  or or_8 (or_8_out, and_9_out, and_3_out);
  or or_9 (or_9_out, or_7_out, or_8_out);
  or or_10 (C4, or_5_out, or_6_out);
  xor xor_5 (S0, xor_1_out, C0);
  xor xor_6 (S1, or_2_out, xor_2_out);
  xor xor_7 (S2, or_4_out, xor_3_out);
  xor xor_8 (S3, xor_4_out, or_9_out);
endmodule
