// Logisim project 实验3-ACM1801-U201814565-王家璇-1.circ as structural Verilog: 15 circuits, main circuit 四位乘法器
module \四位乘法器  (
  input  [3:0] A,
  input  [3:0] B,
  output [7:0] out_3
);

  wire [7:0] adder_1_out, adder_2_out, adder_3_out, adder_4_out, multiplexer_1_out, multiplexer_2_out,
       multiplexer_3_out, shifter_1_out, shifter_2_out;

  Adder #(.width(8)) adder_1 (.a({8{1'b0}}), .b({4'b0000, B}), .out(adder_1_out), .cin(1'b0));  // open: cout
  Multiplexer #(.select(1), .width(8), .disabled("Z"), .enable("false")) multiplexer_1 (
    .in0({8{1'b0}}), .in1(adder_1_out), .out(multiplexer_1_out), .sel(A[0]));
  Adder #(.width(8)) adder_2 (
    .a(multiplexer_1_out), .b({3'b000, B, 1'b0}), .out(adder_2_out), .cin(1'b0));  // open: cout
  Multiplexer #(.select(1), .width(8), .disabled("Z"), .enable("false")) multiplexer_2 (
    .in0(multiplexer_1_out), .in1(adder_2_out), .out(multiplexer_2_out), .sel(A[1]));
  Shifter #(.width(8), .shift("ll")) shifter_1 (.in({3'b000, B, 1'b0}), .\dist (3'b001), .out(shifter_1_out));
  Adder #(.width(8)) adder_3 (.a(multiplexer_2_out), .b(shifter_1_out), .out(adder_3_out), .cin(1'b0));  // open: cout
  Multiplexer #(.select(1), .width(8), .disabled("Z"), .enable("false")) multiplexer_3 (
    .in0(multiplexer_2_out), .in1(adder_3_out), .out(multiplexer_3_out), .sel(A[2]));
  Shifter #(.width(8), .shift("ll")) shifter_2 (.in(shifter_1_out), .\dist (3'b001), .out(shifter_2_out));
  Adder #(.width(8)) adder_4 (.a(multiplexer_3_out), .b(shifter_2_out), .out(adder_4_out), .cin(1'b0));  // open: cout
  Multiplexer #(.select(1), .width(8), .disabled("Z"), .enable("false")) multiplexer_4 (
    .in0(multiplexer_3_out), .in1(adder_4_out), .out(out_3), .sel(A[3]));

  // Notes on the sheet:
  //   输入B扩充为8位
  //   设计思想：利用乘法的定义，将一个被乘数拆解为不同的单位，每一位有不同的权值，根据该位是否为1决定是否加上对应该权值移位的另一个乘数，并将得数作为积的一部分继续该过程
endmodule

module \四位乘法器测试电路  (
  input  [3:0] in_1,
  input  [3:0] in_2,
  output [7:0] out_3
);

  \四位乘法器  \u_四位乘法器_1  (.A(in_1), .B(in_2), .out_3(out_3));
endmodule

module \_32X4乘法器  (
  input  [3:0] A,
  input  [31:0] \B低32 ,
  output [31:0] \输出高 ,
  output [31:0] \输出低 
);

  wire [31:0] \n64位加法器_1_输出低 , \n64位加法器_1_输出高 , \n64位加法器_2_输出低 , \n64位加法器_2_输出高 , \n64位加法器_3_输出低 ,
       \n64位加法器_3_输出高 , \n64位加法器_4_输出低 , \n64位加法器_4_输出高 , \n64位多路选择器_1_p低 , \n64位多路选择器_1_p高 ,
       \n64位多路选择器_2_p低 , \n64位多路选择器_2_p高 , \n64位多路选择器_3_p低 , \n64位多路选择器_3_p高 ;

  \_64位加法器  \u_64位加法器_1  (
    .\A低 ({32{1'b0}}), .\B低 (\B低32 ), .\A高 ({32{1'b0}}), .\B高 ({32{1'b0}}), .\输出低 (\n64位加法器_1_输出低 ),
    .\输出高 (\n64位加法器_1_输出高 ));
  \_64位多路选择器  \u_64位多路选择器_1  (
    .\A高 ({32{1'b0}}), .\B高 (\n64位加法器_1_输出高 ), .\A低 ({32{1'b0}}), .\B低 (\n64位加法器_1_输出低 ),
    .\p高 (\n64位多路选择器_1_p高 ), .in_3(A[0]), .\p低 (\n64位多路选择器_1_p低 ));
  \_64位加法器  \u_64位加法器_2  (
    .\A低 (\n64位多路选择器_1_p低 ), .\B低 ({\B低32 [30:0], 1'b0}), .\A高 (\n64位多路选择器_1_p高 ),
    .\B高 ({{31{1'b0}}, \B低32 [31]}), .\输出低 (\n64位加法器_2_输出低 ), .\输出高 (\n64位加法器_2_输出高 ));
  \_64位多路选择器  \u_64位多路选择器_2  (
    .\A高 (\n64位多路选择器_1_p高 ), .\B高 (\n64位加法器_2_输出高 ), .\A低 (\n64位多路选择器_1_p低 ), .\B低 (\n64位加法器_2_输出低 ),
    .\p高 (\n64位多路选择器_2_p高 ), .in_3(A[1]), .\p低 (\n64位多路选择器_2_p低 ));
  \_64位加法器  \u_64位加法器_3  (
    .\A低 (\n64位多路选择器_2_p低 ), .\B低 ({\B低32 [29:0], 2'b00}), .\A高 (\n64位多路选择器_2_p高 ),
    .\B高 ({{30{1'b0}}, \B低32 [31:30]}), .\输出低 (\n64位加法器_3_输出低 ), .\输出高 (\n64位加法器_3_输出高 ));
  \_64位多路选择器  \u_64位多路选择器_3  (
    .\A高 (\n64位多路选择器_2_p高 ), .\B高 (\n64位加法器_3_输出高 ), .\A低 (\n64位多路选择器_2_p低 ), .\B低 (\n64位加法器_3_输出低 ),
    .\p高 (\n64位多路选择器_3_p高 ), .in_3(A[2]), .\p低 (\n64位多路选择器_3_p低 ));
  \_64位加法器  \u_64位加法器_4  (
    .\A低 (\n64位多路选择器_3_p低 ), .\B低 ({\B低32 [28:0], 3'b000}), .\A高 (\n64位多路选择器_3_p高 ),
    .\B高 ({{29{1'b0}}, \B低32 [31:29]}), .\输出低 (\n64位加法器_4_输出低 ), .\输出高 (\n64位加法器_4_输出高 ));
  \_64位多路选择器  \u_64位多路选择器_4  (
    .\A高 (\n64位多路选择器_3_p高 ), .\B高 (\n64位加法器_4_输出高 ), .\A低 (\n64位多路选择器_3_p低 ), .\B低 (\n64位加法器_4_输出低 ),
    .\p高 (\输出高 ), .in_3(A[3]), .\p低 (\输出低 ));

  // Notes on the sheet:
  //   设计思想：于四位乘法器相同，但将主干部分的数据通路拓宽为64位
endmodule

module \_32X4乘法器测试电路  (
  input  [3:0] in_1,
  input  [31:0] in_2,
  output [31:0] out_3,
  output [31:0] out_4
);

  \_32X4乘法器  \u_32x4乘法器_1  (.A(in_1), .\B低32 (in_2), .\输出低 (out_4), .\输出高 (out_3));
endmodule

module \_32X32乘法器  (
  input  [31:0] a,
  input  [31:0] b,
  output [31:0] \高32位输出 ,
  output [31:0] \低32位输出 
);

  wire [31:0] \n32x4乘法器_1_输出低 , \n32x4乘法器_1_输出高 , \n32x4乘法器_2_输出低 , \n32x4乘法器_2_输出高 , \n32x4乘法器_3_输出低 ,
       \n32x4乘法器_3_输出高 , \n32x4乘法器_4_输出低 , \n32x4乘法器_4_输出高 , \n32x4乘法器_5_输出低 , \n32x4乘法器_5_输出高 ,
       \n32x4乘法器_6_输出低 , \n32x4乘法器_6_输出高 , \n32x4乘法器_7_输出低 , \n32x4乘法器_7_输出高 , \n32x4乘法器_8_输出低 ,
       \n32x4乘法器_8_输出高 , \n64位加法器_1_输出低 , \n64位加法器_1_输出高 , \n64位加法器_2_输出低 , \n64位加法器_2_输出高 , \n64位加法器_3_输出低 ,
       \n64位加法器_3_输出高 , \n64位加法器_4_输出低 , \n64位加法器_4_输出高 , \n64位加法器_5_输出低 , \n64位加法器_5_输出高 , \n64位加法器_6_输出低 ,
       \n64位加法器_6_输出高 , \n64位加法器_7_输出低 , \n64位加法器_7_输出高 , \移4_1_out_3 , \移4_1_out_4 , \移8_1_out_3 ,
       \移8_1_out_4 , \移12_1_out_3 , \移12_1_out_4 , \移16_1_out_3 , \移16_1_out_4 , \移20_1_out_3 ,
       \移20_1_out_4 , \移24_1_out_3 , \移24_1_out_4 , \移28_1_out_3 , \移28_1_out_4 ;

  \_32X4乘法器  \u_32x4乘法器_1  (.A(a[3:0]), .\B低32 (b), .\输出低 (\n32x4乘法器_1_输出低 ), .\输出高 (\n32x4乘法器_1_输出高 ));
  \_32X4乘法器  \u_32x4乘法器_2  (.A(a[19:16]), .\B低32 (b), .\输出低 (\n32x4乘法器_2_输出低 ), .\输出高 (\n32x4乘法器_2_输出高 ));
  \移16  \u_移16_1  (.\低32位 (\n32x4乘法器_2_输出低 ), .\高32位 (\n32x4乘法器_2_输出高 ), .out_3(\移16_1_out_3 ), .out_4(\移16_1_out_4 ));
  \_64位加法器  \u_64位加法器_1  (
    .\A低 ({32{1'b0}}), .\B低 (\n32x4乘法器_1_输出低 ), .\A高 ({32{1'b0}}), .\B高 (\n32x4乘法器_1_输出高 ),
    .\输出低 (\n64位加法器_1_输出低 ), .\输出高 (\n64位加法器_1_输出高 ));
  \_64位加法器  \u_64位加法器_2  (
    .\A低 (\n64位加法器_7_输出低 ), .\B低 (\移16_1_out_3 ), .\A高 (\n64位加法器_7_输出高 ), .\B高 (\移16_1_out_4 ),
    .\输出低 (\n64位加法器_2_输出低 ), .\输出高 (\n64位加法器_2_输出高 ));
  \_32X4乘法器  \u_32x4乘法器_3  (.A(a[7:4]), .\B低32 (b), .\输出低 (\n32x4乘法器_3_输出低 ), .\输出高 (\n32x4乘法器_3_输出高 ));
  \_32X4乘法器  \u_32x4乘法器_4  (.A(a[23:20]), .\B低32 (b), .\输出低 (\n32x4乘法器_4_输出低 ), .\输出高 (\n32x4乘法器_4_输出高 ));
  \移4  \u_移4_1  (.\低32位 (\n32x4乘法器_3_输出低 ), .\高32位 (\n32x4乘法器_3_输出高 ), .out_3(\移4_1_out_3 ), .out_4(\移4_1_out_4 ));
  \移20  \u_移20_1  (.\低32位 (\n32x4乘法器_4_输出低 ), .\高32位 (\n32x4乘法器_4_输出高 ), .out_3(\移20_1_out_3 ), .out_4(\移20_1_out_4 ));
  \_64位加法器  \u_64位加法器_3  (
    .\A低 (\n64位加法器_1_输出低 ), .\B低 (\移4_1_out_3 ), .\A高 (\n64位加法器_1_输出高 ), .\B高 (\移4_1_out_4 ),
    .\输出低 (\n64位加法器_3_输出低 ), .\输出高 (\n64位加法器_3_输出高 ));
  \_64位加法器  \u_64位加法器_4  (
    .\A低 (\n64位加法器_2_输出低 ), .\B低 (\移20_1_out_3 ), .\A高 (\n64位加法器_2_输出高 ), .\B高 (\移20_1_out_4 ),
    .\输出低 (\n64位加法器_4_输出低 ), .\输出高 (\n64位加法器_4_输出高 ));
  \_32X4乘法器  \u_32x4乘法器_5  (.A(a[11:8]), .\B低32 (b), .\输出低 (\n32x4乘法器_5_输出低 ), .\输出高 (\n32x4乘法器_5_输出高 ));
  \_32X4乘法器  \u_32x4乘法器_6  (.A(a[27:24]), .\B低32 (b), .\输出低 (\n32x4乘法器_6_输出低 ), .\输出高 (\n32x4乘法器_6_输出高 ));
  \移8  \u_移8_1  (.\低32位 (\n32x4乘法器_5_输出低 ), .\高32位 (\n32x4乘法器_5_输出高 ), .out_3(\移8_1_out_3 ), .out_4(\移8_1_out_4 ));
  \移24  \u_移24_1  (.\低32位 (\n32x4乘法器_6_输出低 ), .\高32位 (\n32x4乘法器_6_输出高 ), .out_3(\移24_1_out_3 ), .out_4(\移24_1_out_4 ));
  \_64位加法器  \u_64位加法器_5  (
    .\A低 (\n64位加法器_3_输出低 ), .\B低 (\移8_1_out_3 ), .\A高 (\n64位加法器_3_输出高 ), .\B高 (\移8_1_out_4 ),
    .\输出低 (\n64位加法器_5_输出低 ), .\输出高 (\n64位加法器_5_输出高 ));
  \_64位加法器  \u_64位加法器_6  (
    .\A低 (\n64位加法器_4_输出低 ), .\B低 (\移24_1_out_3 ), .\A高 (\n64位加法器_4_输出高 ), .\B高 (\移24_1_out_4 ),
    .\输出低 (\n64位加法器_6_输出低 ), .\输出高 (\n64位加法器_6_输出高 ));
  \_32X4乘法器  \u_32x4乘法器_7  (.A(a[15:12]), .\B低32 (b), .\输出低 (\n32x4乘法器_7_输出低 ), .\输出高 (\n32x4乘法器_7_输出高 ));
  \_32X4乘法器  \u_32x4乘法器_8  (.A(a[31:28]), .\B低32 (b), .\输出低 (\n32x4乘法器_8_输出低 ), .\输出高 (\n32x4乘法器_8_输出高 ));
  \移12  \u_移12_1  (.\低32位 (\n32x4乘法器_7_输出低 ), .\高32位 (\n32x4乘法器_7_输出高 ), .out_3(\移12_1_out_3 ), .out_4(\移12_1_out_4 ));
  \移28  \u_移28_1  (.\低32位 (\n32x4乘法器_8_输出低 ), .\高32位 (\n32x4乘法器_8_输出高 ), .out_3(\移28_1_out_3 ), .out_4(\移28_1_out_4 ));
  \_64位加法器  \u_64位加法器_7  (
    .\A低 (\n64位加法器_5_输出低 ), .\B低 (\移12_1_out_3 ), .\A高 (\n64位加法器_5_输出高 ), .\B高 (\移12_1_out_4 ),
    .\输出低 (\n64位加法器_7_输出低 ), .\输出高 (\n64位加法器_7_输出高 ));
  \_64位加法器  \u_64位加法器_8  (
    .\A低 (\n64位加法器_6_输出低 ), .\B低 (\移28_1_out_3 ), .\A高 (\n64位加法器_6_输出高 ), .\B高 (\移28_1_out_4 ),
    .\输出低 (\低32位输出 ), .\输出高 (\高32位输出 ));

  // Notes on the sheet:
  //   设计思想：将一个被乘数每4位一组拆解成8组，每组分别用32X4乘法器与另一个乘数相乘，然后按照该组拆解前的权值进行位移后求和
endmodule

module \_32X32乘法器测试电路  (
  input  [31:0] in_1,
  input  [31:0] in_2,
  output [31:0] out_3,
  output [31:0] out_4
);

  \_32X32乘法器  \u_32x32乘法器_1  (.a(in_1), .b(in_2), .\高32位输出 (out_3), .\低32位输出 (out_4));
endmodule

module \_64位加法器  (
  input  [31:0] \A低 ,
  input  [31:0] \B低 ,
  input  [31:0] \A高 ,
  input  [31:0] \B高 ,
  output [31:0] \输出低 ,
  output [31:0] \输出高 
);

  wire adder_1_cout;

  Adder #(.width(32)) adder_1 (.a(\A低 ), .b(\B低 ), .out(\输出低 ), .cin(1'b0), .cout(adder_1_cout));
  Adder #(.width(32)) adder_2 (.a(\A高 ), .b(\B高 ), .out(\输出高 ), .cin(adder_1_cout));  // open: cout
endmodule

module \_64位多路选择器  (
  input  [31:0] \A高 ,
  input  [31:0] \B高 ,
  input  in_3,
  input  [31:0] \A低 ,
  input  [31:0] \B低 ,
  output [31:0] \p高 ,
  output [31:0] \p低 
);

  Multiplexer #(.select(1), .width(32), .disabled("Z"), .enable("false")) multiplexer_1 (
    .in0(\A高 ), .in1(\B高 ), .out(\p高 ), .sel(in_3));
  Multiplexer #(.select(1), .width(32), .disabled("Z"), .enable("false")) multiplexer_2 (
    .in0(\A低 ), .in1(\B低 ), .out(\p低 ), .sel(in_3));
endmodule

module \移4  (
  input  [31:0] \低32位 ,
  input  [31:0] \高32位 ,
  output [31:0] out_3,
  output [31:0] out_4
);


  assign out_3 = {\低32位 [27:0], 4'b0000};
  assign out_4 = {\高32位 [27:0], \低32位 [31:28]};
endmodule

module \移8  (
  input  [31:0] \低32位 ,
  input  [31:0] \高32位 ,
  output [31:0] out_3,
  output [31:0] out_4
);


  assign out_3 = {\低32位 [23:0], {8{1'b0}}};
  assign out_4 = {\高32位 [23:0], \低32位 [31:24]};
endmodule

module \移12  (
  input  [31:0] \低32位 ,
  input  [31:0] \高32位 ,
  output [31:0] out_3,
  output [31:0] out_4
);


  assign out_3 = {\低32位 [19:0], {12{1'b0}}};
  assign out_4 = {\高32位 [19:0], \低32位 [31:20]};
endmodule

module \移16  (
  input  [31:0] \低32位 ,
  input  [31:0] \高32位 ,
  output [31:0] out_3,
  output [31:0] out_4
);


  assign out_3 = {\低32位 [15:0], {16{1'b0}}};
  assign out_4 = {\高32位 [15:0], \低32位 [31:16]};
endmodule

module \移20  (
  input  [31:0] \低32位 ,
  input  [31:0] \高32位 ,
  output [31:0] out_3,
  output [31:0] out_4
);


  assign out_3 = {\低32位 [11:0], {20{1'b0}}};
  assign out_4 = {\高32位 [11:0], \低32位 [31:12]};
endmodule

module \移24  (
  input  [31:0] \低32位 ,
  input  [31:0] \高32位 ,
  output [31:0] out_3,
  output [31:0] out_4
);


  assign out_3 = {\低32位 [7:0], {24{1'b0}}};
  assign out_4 = {\高32位 [7:0], \低32位 [31:8]};
endmodule

module \移28  (
  input  [31:0] \低32位 ,
  input  [31:0] \高32位 ,
  output [31:0] out_3,
  output [31:0] out_4
);


  assign out_3 = {\低32位 [3:0], {28{1'b0}}};
  assign out_4 = {\高32位 [3:0], \低32位 [31:4]};
endmodule
