// Logisim project 实验4-ACM1801-U201814565-王家璇.circ as structural Verilog: 6 circuits, main circuit 四位除法器
module \四位除法器  (
  input  [3:0] n2,
  input  [3:0] d,
  output [3:0] quot,
  output [3:0] rem
);

  wire comparator_1_eq, comparator_1_gt, comparator_2_eq, comparator_2_gt, comparator_3_eq, comparator_3_gt,
       comparator_4_eq, comparator_4_gt, or_1_out, or_2_out, or_3_out, or_4_out;
  wire [3:0] multiplexer_1_out, multiplexer_2_out, multiplexer_3_out, multiplexer_4_out, multiplexer_5_out,
       multiplexer_6_out, subtractor_1_out, subtractor_2_out, subtractor_3_out, subtractor_4_out;
  wire [7:0] shifter_1_out, shifter_2_out, shifter_3_out, shifter_4_out;

  Shifter #(.width(8), .shift("ll")) shifter_1 (.in({4'b0000, n2}), .\dist (3'b001), .out(shifter_1_out));
  or or_1 (or_1_out, comparator_1_gt, comparator_1_eq);
  Comparator #(.width(4), .mode("unsigned")) comparator_1 (
    .a(shifter_1_out[7:4]), .b(d), .gt(comparator_1_gt), .eq(comparator_1_eq));  // open: lt
  Subtractor #(.width(4)) subtractor_1 (
    .a(shifter_1_out[7:4]), .b(d), .out(subtractor_1_out), .bin(1'b0));  // open: bout
  Multiplexer #(.select(1), .width(4), .disabled("Z"), .enable("false")) multiplexer_1 (
    .in0(shifter_1_out[3:0]), .in1({shifter_1_out[3:1], 1'b1}), .out(multiplexer_1_out), .sel(or_1_out));
  Multiplexer #(.select(1), .width(4), .disabled("Z"), .enable("false")) multiplexer_2 (
    .in0(shifter_1_out[7:4]), .in1(subtractor_1_out), .out(multiplexer_2_out), .sel(or_1_out));
  Shifter #(.width(8), .shift("ll")) shifter_2 (
    .in({multiplexer_2_out, multiplexer_1_out}), .\dist (3'b001), .out(shifter_2_out));
  Comparator #(.width(4), .mode("unsigned")) comparator_2 (
    .a(shifter_2_out[7:4]), .b(d), .gt(comparator_2_gt), .eq(comparator_2_eq));  // open: lt
  Subtractor #(.width(4)) subtractor_2 (
    .a(shifter_2_out[7:4]), .b(d), .out(subtractor_2_out), .bin(1'b0));  // open: bout
  or or_2 (or_2_out, comparator_2_gt, comparator_2_eq);
  Multiplexer #(.select(1), .width(4), .disabled("Z"), .enable("false")) multiplexer_3 (
    .in0(shifter_2_out[3:0]), .in1({shifter_2_out[3:1], 1'b1}), .out(multiplexer_3_out), .sel(or_2_out));
  Multiplexer #(.select(1), .width(4), .disabled("Z"), .enable("false")) multiplexer_4 (
    .in0(shifter_2_out[7:4]), .in1(subtractor_2_out), .out(multiplexer_4_out), .sel(or_2_out));
  Shifter #(.width(8), .shift("ll")) shifter_3 (
    .in({multiplexer_4_out, multiplexer_3_out}), .\dist (3'b001), .out(shifter_3_out));
  or or_3 (or_3_out, comparator_3_gt, comparator_3_eq);
  Comparator #(.width(4), .mode("unsigned")) comparator_3 (
    .a(shifter_3_out[7:4]), .b(d), .gt(comparator_3_gt), .eq(comparator_3_eq));  // open: lt
  Subtractor #(.width(4)) subtractor_3 (
    .a(shifter_3_out[7:4]), .b(d), .out(subtractor_3_out), .bin(1'b0));  // open: bout
  Multiplexer #(.select(1), .width(4), .disabled("Z"), .enable("false")) multiplexer_5 (
    .in0(shifter_3_out[3:0]), .in1({shifter_3_out[3:1], 1'b1}), .out(multiplexer_5_out), .sel(or_3_out));
  Multiplexer #(.select(1), .width(4), .disabled("Z"), .enable("false")) multiplexer_6 (
    .in0(shifter_3_out[7:4]), .in1(subtractor_3_out), .out(multiplexer_6_out), .sel(or_3_out));
  Shifter #(.width(8), .shift("ll")) shifter_4 (
    .in({multiplexer_6_out, multiplexer_5_out}), .\dist (3'b001), .out(shifter_4_out));
  Comparator #(.width(4), .mode("unsigned")) comparator_4 (
    .a(shifter_4_out[7:4]), .b(d), .gt(comparator_4_gt), .eq(comparator_4_eq));  // open: lt
  Subtractor #(.width(4)) subtractor_4 (
    .a(shifter_4_out[7:4]), .b(d), .out(subtractor_4_out), .bin(1'b0));  // open: bout
  or or_4 (or_4_out, comparator_4_gt, comparator_4_eq);
  Multiplexer #(.select(1), .width(4), .disabled("Z"), .enable("false")) multiplexer_7 (
    .in0(shifter_4_out[3:0]), .in1({shifter_4_out[3:1], 1'b1}), .out(quot), .sel(or_4_out));
  Multiplexer #(.select(1), .width(4), .disabled("Z"), .enable("false")) multiplexer_8 (
    .in0(shifter_4_out[7:4]), .in1(subtractor_4_out), .out(rem), .sel(or_4_out));

  // Notes on the sheet:
  //   设计思想：按照扩展-移位-比较-计算-循环的除法器设计思想，针对输入的四位操作数，共设计四段电路，通过四段电路中数据的依次迭代实现四次循环，从而实现四位无符号整数的除法
endmodule

module \四位除法器测试电路  (
  input  [3:0] in_1,
  input  [3:0] in_2,
  output [3:0] out_3,
  output [3:0] out_4
);

  \四位除法器  \u_四位除法器_1  (.n2(in_1), .d(in_2), .quot(out_3), .rem(out_4));
endmodule

module \_32位除法器  (
  input  [31:0] in_1,
  input  [31:0] in_2,
  output [31:0] out_3,
  output [31:0] out_4
);

  wire [31:0] div1_1_out_4, div1_1_out_5, div1_2_out_4, div1_2_out_5, div1_3_out_4, div1_3_out_5,
       div1_4_out_4, div1_4_out_5, div1_5_out_4, div1_5_out_5, div1_6_out_4, div1_6_out_5, div1_7_out_4,
       div1_7_out_5, div1_8_out_4, div1_8_out_5, div1_9_out_4, div1_9_out_5, div1_10_out_4, div1_10_out_5,
       div1_11_out_4, div1_11_out_5, div1_12_out_4, div1_12_out_5, div1_13_out_4, div1_13_out_5,
       div1_14_out_4, div1_14_out_5, div1_15_out_4, div1_15_out_5, div1_16_out_4, div1_16_out_5,
       div1_17_out_4, div1_17_out_5, div1_18_out_4, div1_18_out_5, div1_19_out_4, div1_19_out_5,
       div1_20_out_4, div1_20_out_5, div1_21_out_4, div1_21_out_5, div1_22_out_4, div1_22_out_5,
       div1_23_out_4, div1_23_out_5, div1_24_out_4, div1_24_out_5, div1_25_out_4, div1_25_out_5,
       div1_26_out_4, div1_26_out_5, div1_27_out_4, div1_27_out_5, div1_28_out_4, div1_28_out_5,
       div1_29_out_4, div1_29_out_5, div1_30_out_4, div1_30_out_5, div1_31_out_4, div1_31_out_5;

  Div1 div1_1 (.in_1(in_1), .in_2({32{1'b0}}), .d(in_2), .out_4(div1_1_out_4), .out_5(div1_1_out_5));
  Div1 div1_2 (.in_1(div1_29_out_4), .in_2(div1_29_out_5), .d(in_2), .out_4(div1_2_out_4), .out_5(div1_2_out_5));
  Div1 div1_3 (.in_1(div1_30_out_4), .in_2(div1_30_out_5), .d(in_2), .out_4(div1_3_out_4), .out_5(div1_3_out_5));
  Div1 div1_4 (.in_1(div1_31_out_4), .in_2(div1_31_out_5), .d(in_2), .out_4(div1_4_out_4), .out_5(div1_4_out_5));
  Div1 div1_5 (.in_1(div1_1_out_4), .in_2(div1_1_out_5), .d(in_2), .out_4(div1_5_out_4), .out_5(div1_5_out_5));
  Div1 div1_6 (.in_1(div1_2_out_4), .in_2(div1_2_out_5), .d(in_2), .out_4(div1_6_out_4), .out_5(div1_6_out_5));
  Div1 div1_7 (.in_1(div1_3_out_4), .in_2(div1_3_out_5), .d(in_2), .out_4(div1_7_out_4), .out_5(div1_7_out_5));
  Div1 div1_8 (.in_1(div1_4_out_4), .in_2(div1_4_out_5), .d(in_2), .out_4(div1_8_out_4), .out_5(div1_8_out_5));
  Div1 div1_9 (.in_1(div1_5_out_4), .in_2(div1_5_out_5), .d(in_2), .out_4(div1_9_out_4), .out_5(div1_9_out_5));
  Div1 div1_10 (.in_1(div1_6_out_4), .in_2(div1_6_out_5), .d(in_2), .out_4(div1_10_out_4), .out_5(div1_10_out_5));
  Div1 div1_11 (.in_1(div1_7_out_4), .in_2(div1_7_out_5), .d(in_2), .out_4(div1_11_out_4), .out_5(div1_11_out_5));
  Div1 div1_12 (.in_1(div1_8_out_4), .in_2(div1_8_out_5), .d(in_2), .out_4(div1_12_out_4), .out_5(div1_12_out_5));
  Div1 div1_13 (.in_1(div1_9_out_4), .in_2(div1_9_out_5), .d(in_2), .out_4(div1_13_out_4), .out_5(div1_13_out_5));
  Div1 div1_14 (.in_1(div1_10_out_4), .in_2(div1_10_out_5), .d(in_2), .out_4(div1_14_out_4), .out_5(div1_14_out_5));
  Div1 div1_15 (.in_1(div1_11_out_4), .in_2(div1_11_out_5), .d(in_2), .out_4(div1_15_out_4), .out_5(div1_15_out_5));
  Div1 div1_16 (.in_1(div1_12_out_4), .in_2(div1_12_out_5), .d(in_2), .out_4(div1_16_out_4), .out_5(div1_16_out_5));
  Div1 div1_17 (.in_1(div1_13_out_4), .in_2(div1_13_out_5), .d(in_2), .out_4(div1_17_out_4), .out_5(div1_17_out_5));
  Div1 div1_18 (.in_1(div1_14_out_4), .in_2(div1_14_out_5), .d(in_2), .out_4(div1_18_out_4), .out_5(div1_18_out_5));
  Div1 div1_19 (.in_1(div1_15_out_4), .in_2(div1_15_out_5), .d(in_2), .out_4(div1_19_out_4), .out_5(div1_19_out_5));
  Div1 div1_20 (.in_1(div1_16_out_4), .in_2(div1_16_out_5), .d(in_2), .out_4(div1_20_out_4), .out_5(div1_20_out_5));
  Div1 div1_21 (.in_1(div1_17_out_4), .in_2(div1_17_out_5), .d(in_2), .out_4(div1_21_out_4), .out_5(div1_21_out_5));
  Div1 div1_22 (.in_1(div1_18_out_4), .in_2(div1_18_out_5), .d(in_2), .out_4(div1_22_out_4), .out_5(div1_22_out_5));
  Div1 div1_23 (.in_1(div1_19_out_4), .in_2(div1_19_out_5), .d(in_2), .out_4(div1_23_out_4), .out_5(div1_23_out_5));
  Div1 div1_24 (.in_1(div1_20_out_4), .in_2(div1_20_out_5), .d(in_2), .out_4(div1_24_out_4), .out_5(div1_24_out_5));
  Div1 div1_25 (.in_1(div1_21_out_4), .in_2(div1_21_out_5), .d(in_2), .out_4(div1_25_out_4), .out_5(div1_25_out_5));
  Div1 div1_26 (.in_1(div1_22_out_4), .in_2(div1_22_out_5), .d(in_2), .out_4(div1_26_out_4), .out_5(div1_26_out_5));
  Div1 div1_27 (.in_1(div1_23_out_4), .in_2(div1_23_out_5), .d(in_2), .out_4(div1_27_out_4), .out_5(div1_27_out_5));
  Div1 div1_28 (.in_1(div1_24_out_4), .in_2(div1_24_out_5), .d(in_2), .out_4(div1_28_out_4), .out_5(div1_28_out_5));
  Div1 div1_29 (.in_1(div1_25_out_4), .in_2(div1_25_out_5), .d(in_2), .out_4(div1_29_out_4), .out_5(div1_29_out_5));
  Div1 div1_30 (.in_1(div1_26_out_4), .in_2(div1_26_out_5), .d(in_2), .out_4(div1_30_out_4), .out_5(div1_30_out_5));
  Div1 div1_31 (.in_1(div1_27_out_4), .in_2(div1_27_out_5), .d(in_2), .out_4(div1_31_out_4), .out_5(div1_31_out_5));
  Div1 div1_32 (.in_1(div1_28_out_4), .in_2(div1_28_out_5), .d(in_2), .out_4(out_3), .out_5(out_4));

  // Notes on the sheet:
  //   设计思想：将4位除法器中循环的基本单元改写成支持32位操作数，并封装成Div1后进行32次数据迭代，完成32位操作数的除法运算
endmodule

module \_32位除法器测试电路  (
  input  [31:0] in_1,
  input  [31:0] in_2,
  output [31:0] out_3,
  output [31:0] out_4
);

  \_32位除法器  \u_32位除法器_1  (.in_1(in_1), .in_2(in_2), .out_3(out_3), .out_4(out_4));
endmodule

module Div1 (
  input  [31:0] in_1,
  input  [31:0] in_2,
  input  [31:0] d,
  output [31:0] out_4,
  output [31:0] out_5
);

  wire comparator_1_eq, comparator_1_gt, or_1_out;
  wire [31:0] \n64位左移1_1_出低32 , \n64位左移1_1_出高32 , subtractor_1_out;

  \_64位左移1  \u_64位左移1_1  (.\入低32 (in_1), .\入高32 (in_2), .\出低32 (\n64位左移1_1_出低32 ), .\出高32 (\n64位左移1_1_出高32 ));
  or or_1 (or_1_out, comparator_1_gt, comparator_1_eq);
  Comparator #(.width(32), .mode("unsigned")) comparator_1 (
    .a(\n64位左移1_1_出高32 ), .b(d), .gt(comparator_1_gt), .eq(comparator_1_eq));  // open: lt
  Multiplexer #(.select(1), .width(32), .disabled("Z"), .enable("false")) multiplexer_1 (
    .in0(\n64位左移1_1_出高32 ), .in1(subtractor_1_out), .out(out_5), .sel(or_1_out));
  Subtractor #(.width(32)) subtractor_1 (
    .a(\n64位左移1_1_出高32 ), .b(d), .out(subtractor_1_out), .bin(1'b0));  // open: bout
  Multiplexer #(.select(1), .width(32), .disabled("Z"), .enable("false")) multiplexer_2 (
    .in0(\n64位左移1_1_出低32 ), .in1({\n64位左移1_1_出低32 [31:1], 1'b1}), .out(out_4), .sel(or_1_out));
endmodule

module \_64位左移1  (
  input  [31:0] \入低32 ,
  input  [31:0] \入高32 ,
  output [31:0] \出低32 ,
  output [31:0] \出高32 
);


  assign \出低32  = {\入低32 [30:0], 1'b0};
  assign \出高32  = {\入高32 [30:0], \入低32 [31]};
endmodule
