// Logisim project 实验5-ACM1801-U201814565-王家璇.circ as structural Verilog: 14 circuits, main circuit 四位二进制可逆计数器
module \六十进制计数器  (
  input  CPu,
  input  CPd,
  input  Adj,
  input  CLR,
  output \Qcc拔 ,
  output Q1D,
  output out_7,
  output Q1B,
  output Q1A,
  output Q0D,
  output Q0C,
  output Q0B,
  output Q0A
);

  wire and_1_out, and_2_out, and_4_out, and_5_out, and_6_out, and_7_out, and_8_out, and_9_out, and_10_out,
       and_11_out, buffer_1_out, buffer_2_out, not_1_out, not_2_out, not_3_out, not_4_out, or_1_out,
       or_2_out, or_3_out, or_4_out, or_5_out, or_6_out, or_7_out, or_8_out, or_9_out, or_10_out;

  or or_1 (or_1_out, Q0D, Q0C);
  or or_2 (or_2_out, Q0B, Q0A);
  or or_3 (or_3_out, or_1_out, or_2_out);
  or or_4 (or_4_out, or_3_out, or_9_out);
  and and_1 (and_1_out, CPd, Adj);
  or or_5 (or_5_out, and_9_out, and_11_out);
  or or_6 (or_6_out, or_5_out, CLR);
  and and_2 (and_2_out, or_4_out, and_1_out);
  \四位二进制可逆计数器  \u_四位二进制可逆计数器_1  (
    .D(1'b1), .C(1'b0), .B(1'b0), .A(1'b1), .out_9(Q0D), .out_10(Q0C), .out_11(Q0B), .out_12(Q0A),
    .\LD拔 (not_4_out), .CPu(CPu), .CPd(and_2_out), .CLR(or_6_out));
  and and_3 (\Qcc拔 , not_1_out, and_11_out);
  not not_1 (not_1_out, Adj);
  and and_4 (and_4_out, Q0A, Q0C);
  and and_5 (and_5_out, Q0B, Q0D);
  buf buffer_1 (buffer_1_out, Q0B);
  and and_6 (and_6_out, buffer_1_out, buffer_2_out);
  buf buffer_2 (buffer_2_out, Q0D);
  not not_2 (not_2_out, Q0A);
  and and_7 (and_7_out, not_2_out, not_3_out);
  not not_3 (not_3_out, Q0C);
  not not_4 (not_4_out, and_8_out);
  and and_8 (and_8_out, and_4_out, and_5_out);
  and and_9 (and_9_out, and_6_out, and_7_out);
  or or_7 (or_7_out, Q1A, Q1B);
  or or_8 (or_8_out, out_7, Q1D);
  or or_9 (or_9_out, or_7_out, or_8_out);
  or or_10 (or_10_out, and_11_out, CLR);
  and and_10 (and_10_out, or_9_out, and_8_out);
  and and_11 (and_11_out, out_7, Q1B);
  \四位二进制可逆计数器  \u_四位二进制可逆计数器_2  (
    .D(1'b1), .C(1'b1), .B(1'b1), .A(1'b1), .out_9(Q1D), .out_10(out_7), .out_11(Q1B), .out_12(Q1A),
    .\LD拔 (1'b1), .CPu(and_9_out), .CPd(and_10_out), .CLR(or_10_out));

  // Notes on the sheet:
  //   值得注意的是缓冲器的加入，否则会有险象
  //   通过灵活使用置位和使能自订计数器
endmodule

module \四位二进制可逆计数器  (
  input  D,
  input  C,
  input  B,
  input  A,
  input  \LD拔 ,
  input  CPu,
  input  CPd,
  input  CLR,
  output out_9,
  output out_10,
  output out_11,
  output out_12
);

  wire and_1_out, and_2_out, and_3_out, and_4_out, and_5_out, and_6_out, and_7_out, and_8_out, and_9_out,
       and_10_out, and_11_out, and_12_out, and_13_out, and_14_out, and_15_out, and_16_out, and_17_out,
       and_18_out, and_19_out, and_20_out, and_21_out, and_22_out, d_ff_1_qn, d_ff_2_qn, d_ff_3_qn,
       d_ff_4_qn, not_1_out, not_2_out, not_3_out, not_4_out, not_5_out, or_1_out, or_2_out, or_3_out,
       or_4_out, or_5_out, or_6_out, or_7_out, or_8_out;

  not not_1 (not_1_out, D);
  not not_2 (not_2_out, C);
  not not_3 (not_3_out, B);
  not not_4 (not_4_out, A);
  not not_5 (not_5_out, \LD拔 );
  and and_1 (and_1_out, D, not_5_out);
  and and_2 (and_2_out, not_1_out, not_5_out);
  and and_3 (and_3_out, C, not_5_out);
  and and_4 (and_4_out, not_2_out, not_5_out);
  and and_5 (and_5_out, B, not_5_out);
  and and_6 (and_6_out, not_3_out, not_5_out);
  and and_7 (and_7_out, A, not_5_out);
  and and_8 (and_8_out, not_4_out, not_5_out);
  and and_9 (and_9_out, out_11, out_10);
  and and_10 (and_10_out, d_ff_3_qn, d_ff_2_qn);
  and and_11 (and_11_out, CPu, and_12_out);
  and and_12 (and_12_out, out_12, and_9_out);
  and and_13 (and_13_out, CPd, and_14_out);
  and and_14 (and_14_out, d_ff_4_qn, and_10_out);
  and and_15 (and_15_out, CPu, and_16_out);
  and and_16 (and_16_out, out_11, out_12);
  and and_17 (and_17_out, CPd, and_18_out);
  and and_18 (and_18_out, d_ff_3_qn, d_ff_4_qn);
  and and_19 (and_19_out, out_12, CPu);
  and and_20 (and_20_out, d_ff_4_qn, CPd);
  and and_21 (and_21_out, CPu, 1'b1);
  and and_22 (and_22_out, CPd, 1'b1);
  or or_1 (or_1_out, and_11_out, and_13_out);
  or or_2 (or_2_out, and_15_out, and_17_out);
  or or_3 (or_3_out, and_19_out, and_20_out);
  or or_4 (or_4_out, and_21_out, and_22_out);
  D_Flip_Flop #(.trigger("falling"), .Pre_Clr_Positions("ABOVE_BELOW"), .NegatePresetClear("false"), .enable("false"), .NewFFLayout("true")) d_ff_1 (
    .clk(or_1_out), .D(d_ff_1_qn), .Q(out_9), .Qn(d_ff_1_qn), .preset(and_1_out), .reset(or_5_out));
  or or_5 (or_5_out, and_2_out, CLR);
  D_Flip_Flop #(.trigger("falling"), .Pre_Clr_Positions("ABOVE_BELOW"), .NegatePresetClear("false"), .enable("false"), .NewFFLayout("true")) d_ff_2 (
    .clk(or_2_out), .D(d_ff_2_qn), .Q(out_10), .Qn(d_ff_2_qn), .preset(and_3_out), .reset(or_6_out));
  or or_6 (or_6_out, CLR, and_4_out);
  D_Flip_Flop #(.trigger("falling"), .Pre_Clr_Positions("ABOVE_BELOW"), .NegatePresetClear("false"), .enable("false"), .NewFFLayout("true")) d_ff_3 (
    .clk(or_3_out), .D(d_ff_3_qn), .Q(out_11), .Qn(d_ff_3_qn), .preset(and_5_out), .reset(or_7_out));
  or or_7 (or_7_out, and_6_out, CLR);
  D_Flip_Flop #(.trigger("falling"), .Pre_Clr_Positions("ABOVE_BELOW"), .NegatePresetClear("false"), .enable("false"), .NewFFLayout("true")) d_ff_4 (
    .clk(or_4_out), .D(d_ff_4_qn), .Q(out_12), .Qn(d_ff_4_qn), .preset(and_7_out), .reset(or_8_out));
  or or_8 (or_8_out, CLR, and_8_out);
endmodule

module \六十进制计数器测试电路  (
  input  in_1,
  input  in_2,
  input  in_3,
  input  in_4
);

  wire button_1_out, button_2_out, clock_1_out, \六十进制计数器_1_qcc拔 ;
  wire [3:0] \六十进制计数器_1_q0a , \六十进制计数器_1_q1a , \六十进制计数器_2_q0a , \六十进制计数器_2_q1a ;

  Clock #(.highDuration(1), .lowDuration(1)) clock_1 (.out(clock_1_out));
  Hex_Digit_Display hex_digit_display_1 (.value(\六十进制计数器_1_q1a ), .dp(1'b0));
  Button button_1 (.out(button_1_out));
  Hex_Digit_Display hex_digit_display_2 (.value(\六十进制计数器_1_q0a ), .dp(1'b0));
  \六十进制计数器  \u_六十进制计数器_1  (
    .Adj(in_1), .Q0D(\六十进制计数器_1_q0a [3]), .Q0C(\六十进制计数器_1_q0a [2]), .Q0B(\六十进制计数器_1_q0a [1]),
    .Q0A(\六十进制计数器_1_q0a [0]), .\Qcc拔 (\六十进制计数器_1_qcc拔 ), .Q1D(\六十进制计数器_1_q1a [3]),
    .out_7(\六十进制计数器_1_q1a [2]), .Q1B(\六十进制计数器_1_q1a [1]), .Q1A(\六十进制计数器_1_q1a [0]), .CLR(in_3),
    .CPu(clock_1_out), .CPd(button_1_out));
  Button button_2 (.out(button_2_out));
  Hex_Digit_Display hex_digit_display_3 (.value(\六十进制计数器_2_q1a ), .dp(1'b0));
  Hex_Digit_Display hex_digit_display_4 (.value(\六十进制计数器_2_q0a ), .dp(1'b0));
  \六十进制计数器  \u_六十进制计数器_2  (
    .Adj(in_2), .Q0D(\六十进制计数器_2_q0a [3]), .Q0C(\六十进制计数器_2_q0a [2]), .Q0B(\六十进制计数器_2_q0a [1]),
    .Q0A(\六十进制计数器_2_q0a [0]), .Q1D(\六十进制计数器_2_q1a [3]), .out_7(\六十进制计数器_2_q1a [2]), .Q1B(\六十进制计数器_2_q1a [1]),
    .Q1A(\六十进制计数器_2_q1a [0]), .CLR(in_4), .CPu(\六十进制计数器_1_qcc拔 ), .CPd(button_2_out));  // open: Qcc拔

  // Notes on the sheet:
  //   右侧电路用于验证左侧计数器在ADj=0时的进位输出
endmodule

module \十二进制计数器或二十四进制的计数器测试电路  (
  input  in_1,
  input  in_2,
  input  in_3,
  input  in_4,
  input  in_5,
  input  in_6
);

  wire button_1_out, button_2_out, button_3_out, \十二进制计数器或二十四进制的计数器电路_1_qcc拔 ;
  wire [3:0] \十二进制计数器或二十四进制的计数器电路_1_q0a , \十二进制计数器或二十四进制的计数器电路_1_q1a , \十二进制计数器或二十四进制的计数器电路_2_q0a ,
       \十二进制计数器或二十四进制的计数器电路_2_q1a ;

  Hex_Digit_Display hex_digit_display_1 (.value(\十二进制计数器或二十四进制的计数器电路_1_q1a ));  // open: dp
  Button button_1 (.out(button_1_out));
  Button button_2 (.out(button_2_out));
  Hex_Digit_Display hex_digit_display_2 (.value(\十二进制计数器或二十四进制的计数器电路_1_q0a ));  // open: dp
  \十二进制计数器或二十四进制的计数器电路  \u_十二进制计数器或二十四进制的计数器电路_1  (
    .SET(in_2), .CPu(button_1_out), .CPd(button_2_out), .Adj(in_1), .Q0A(\十二进制计数器或二十四进制的计数器电路_1_q0a [0]),
    .Q0B(\十二进制计数器或二十四进制的计数器电路_1_q0a [1]), .Q0C(\十二进制计数器或二十四进制的计数器电路_1_q0a [2]),
    .Q0D(\十二进制计数器或二十四进制的计数器电路_1_q0a [3]), .Q1A(\十二进制计数器或二十四进制的计数器电路_1_q1a [0]),
    .Q1B(\十二进制计数器或二十四进制的计数器电路_1_q1a [1]), .Q1C(\十二进制计数器或二十四进制的计数器电路_1_q1a [2]),
    .Q1D(\十二进制计数器或二十四进制的计数器电路_1_q1a [3]), .\Qcc拔 (\十二进制计数器或二十四进制的计数器电路_1_qcc拔 ), .CLR(in_5));
  Hex_Digit_Display hex_digit_display_3 (.value(\十二进制计数器或二十四进制的计数器电路_2_q1a ));  // open: dp
  Button button_3 (.out(button_3_out));
  Hex_Digit_Display hex_digit_display_4 (.value(\十二进制计数器或二十四进制的计数器电路_2_q0a ));  // open: dp
  \十二进制计数器或二十四进制的计数器电路  \u_十二进制计数器或二十四进制的计数器电路_2  (
    .SET(in_4), .CPu(\十二进制计数器或二十四进制的计数器电路_1_qcc拔 ), .CPd(button_3_out), .Adj(in_3),
    .Q0A(\十二进制计数器或二十四进制的计数器电路_2_q0a [0]), .Q0B(\十二进制计数器或二十四进制的计数器电路_2_q0a [1]),
    .Q0C(\十二进制计数器或二十四进制的计数器电路_2_q0a [2]), .Q0D(\十二进制计数器或二十四进制的计数器电路_2_q0a [3]),
    .Q1A(\十二进制计数器或二十四进制的计数器电路_2_q1a [0]), .Q1B(\十二进制计数器或二十四进制的计数器电路_2_q1a [1]),
    .Q1C(\十二进制计数器或二十四进制的计数器电路_2_q1a [2]), .Q1D(\十二进制计数器或二十四进制的计数器电路_2_q1a [3]), .CLR(in_6));  // open: Qcc拔
endmodule

module \十二进制计数器或二十四进制的计数器电路  (
  input  SET,
  input  CPu,
  input  CPd,
  input  Adj,
  input  CLR,
  output Q0A,
  output Q0B,
  output Q0C,
  output Q0D,
  output Q1A,
  output Q1B,
  output Q1C,
  output Q1D,
  output \Qcc拔 
);

  wire and_1_out, and_2_out, and_3_out, and_4_out, and_5_out, and_6_out, and_7_out, and_8_out, and_9_out,
       and_10_out, and_11_out, and_12_out, and_13_out, and_14_out, and_15_out, and_16_out, and_17_out,
       and_18_out, and_19_out, and_20_out, and_21_out, and_22_out, and_23_out, and_24_out, and_25_out,
       buffer_1_out, buffer_2_out, buffer_3_out, multiplexer_1_out, not_1_out, not_2_out, not_3_out,
       not_4_out, not_5_out, not_6_out, not_7_out, not_8_out, not_9_out, not_10_out, not_11_out, not_12_out,
       not_13_out, not_14_out, not_15_out, or_1_out, or_2_out, or_3_out, or_4_out, or_5_out, or_6_out,
       or_7_out, or_8_out, or_9_out, or_10_out;
  wire [4:0] plarom_1_p2;
  wire [7:0] plarom_1_p1;

  not not_1 (not_1_out, and_1_out);
  and and_1 (and_1_out, plarom_1_p2[0], and_3_out);
  or or_1 (or_1_out, plarom_1_p1[4], plarom_1_p1[5]);
  or or_2 (or_2_out, or_1_out, or_3_out);
  or or_3 (or_3_out, plarom_1_p1[6], plarom_1_p1[7]);
  and and_2 (and_2_out, CPd, Adj);
  and and_3 (and_3_out, and_5_out, and_6_out);
  or or_4 (or_4_out, or_2_out, or_10_out);
  and and_4 (and_4_out, not_1_out, and_2_out);
  and and_5 (and_5_out, not_2_out, not_3_out);
  and and_6 (and_6_out, plarom_1_p2[3], not_4_out);
  or or_5 (or_5_out, and_13_out, and_15_out);
  Multiplexer #(.select(1), .width(1), .disabled("Z"), .enable("false")) multiplexer_1 (
    .in0(and_4_out), .in1(and_7_out), .out(multiplexer_1_out), .sel(SET));
  and and_7 (and_7_out, or_4_out, and_2_out);
  not not_2 (not_2_out, plarom_1_p2[1]);
  not not_3 (not_3_out, plarom_1_p2[2]);
  not not_4 (not_4_out, plarom_1_p2[4]);
  or or_6 (or_6_out, or_5_out, CLR);
  \四位二进制可逆计数器  \u_四位二进制可逆计数器_1  (
    .D(1'b1), .C(1'b0), .B(1'b0), .A(1'b1), .out_9(plarom_1_p1[4]), .out_10(plarom_1_p1[5]),
    .out_11(plarom_1_p1[6]), .out_12(plarom_1_p1[7]), .\LD拔 (not_7_out), .CPu(CPu), .CPd(multiplexer_1_out),
    .CLR(or_6_out));
  buf buffer_1 (buffer_1_out, plarom_1_p1[6]);
  buf buffer_2 (buffer_2_out, plarom_1_p1[4]);
  not not_5 (not_5_out, plarom_1_p1[7]);
  not not_6 (not_6_out, plarom_1_p1[5]);
  not not_7 (not_7_out, and_10_out);
  and and_8 (and_8_out, not_8_out, and_15_out);
  not not_8 (not_8_out, Adj);
  and and_9 (and_9_out, plarom_1_p1[7], plarom_1_p1[5]);
  and and_10 (and_10_out, and_9_out, and_11_out);
  and and_11 (and_11_out, plarom_1_p1[6], plarom_1_p1[4]);
  and and_12 (and_12_out, buffer_1_out, buffer_2_out);
  and and_13 (and_13_out, and_12_out, and_14_out);
  and and_14 (and_14_out, not_5_out, not_6_out);
  // PlaRom #(.\and (24), .outputs(5), .Contents("1*8 2 1*8 2 1*6 2 2 1*8 2 1*5 2 1 2 1*6 2 2 1*5 2*3 1*8 2 1*4 2 1 1 2 1*8 2 1*3 2 1*3 2 1*4 2 1 1 2 1*3 2 2 1 1 2 1*5 2 1 2 1*3 2 1 2 1 2 1*4 2 2 1 2 1*3 2*3 1 2 1*6 2 2 1*3 2 1 1 2 2 1*8 2 1 1 2 1*4 2 1*3 2 1*3 2 1 1 2 2 1*3 2 1 1 0 1 0 0 1 1 0*5 1 0*3 1 1 0*5 1 0 0 1 0 1 0*3 1 1 0 0 1*3 0*5 1 0 1 0 0 1 0*5 1 1 0*3 1 0 1 0 0 1 1 0*5 1 0*3 1 1 0*5 1 0 0 1 0 1 0*3 1 1 0 0 1*3 0*5 1 0 1 0 0 1 0*5 1 1 0*3 1"), .Select("low")) plarom_1: pin names not known; wires that end beside it: plarom_1_p1, plarom_1_p2
  or or_7 (or_7_out, plarom_1_p1[3], plarom_1_p1[2]);
  or or_8 (or_8_out, plarom_1_p1[1], plarom_1_p1[0]);
  and and_15 (and_15_out, plarom_1_p1[2], and_16_out);
  and and_16 (and_16_out, and_17_out, and_18_out);
  and and_17 (and_17_out, not_10_out, buffer_3_out);
  not not_9 (not_9_out, plarom_1_p1[6]);
  not not_10 (not_10_out, plarom_1_p1[4]);
  buf buffer_3 (buffer_3_out, plarom_1_p1[5]);
  or or_9 (or_9_out, and_15_out, CLR);
  or or_10 (or_10_out, or_7_out, or_8_out);
  and and_18 (and_18_out, not_9_out, not_11_out);
  not not_11 (not_11_out, plarom_1_p1[7]);
  and and_19 (and_19_out, or_10_out, and_10_out);
  \四位二进制可逆计数器  \u_四位二进制可逆计数器_2  (
    .D(1'b1), .C(1'b1), .B(1'b1), .A(1'b1), .out_9(plarom_1_p1[0]), .out_10(plarom_1_p1[1]),
    .out_11(plarom_1_p1[2]), .out_12(plarom_1_p1[3]), .\LD拔 (1'b1), .CPu(and_13_out), .CPd(and_19_out),
    .CLR(or_9_out));
  Multiplexer #(.select(1), .width(1), .disabled("Z"), .enable("false")) multiplexer_2 (
    .in0(plarom_1_p2[4]), .in1(plarom_1_p1[7]), .out(Q0A), .sel(SET));
  Multiplexer #(.select(1), .width(1), .disabled("Z"), .enable("false")) multiplexer_3 (
    .in0(plarom_1_p2[3]), .in1(plarom_1_p1[6]), .out(Q0B), .sel(SET));
  Multiplexer #(.select(1), .width(1), .disabled("Z"), .enable("false")) multiplexer_4 (
    .in0(plarom_1_p2[2]), .in1(plarom_1_p1[5]), .out(Q0C), .sel(SET));
  Multiplexer #(.select(1), .width(1), .disabled("Z"), .enable("false")) multiplexer_5 (
    .in0(plarom_1_p2[1]), .in1(plarom_1_p1[4]), .out(Q0D), .sel(SET));
  not not_12 (not_12_out, plarom_1_p2[3]);
  Multiplexer #(.select(1), .width(1), .disabled("Z"), .enable("false")) multiplexer_6 (
    .in0(plarom_1_p2[0]), .in1(plarom_1_p1[3]), .out(Q1A), .sel(SET));
  and and_20 (and_20_out, not_12_out, plarom_1_p2[4]);
  not not_13 (not_13_out, plarom_1_p2[1]);
  and and_21 (and_21_out, not_13_out, not_14_out);
  not not_14 (not_14_out, plarom_1_p2[2]);
  Multiplexer #(.select(1), .width(1), .disabled("Z"), .enable("false")) multiplexer_7 (
    .in0(1'b0), .in1(plarom_1_p1[2]), .out(Q1B), .sel(SET));
  and and_22 (and_22_out, plarom_1_p2[0], and_20_out);
  and and_23 (and_23_out, and_21_out, CPu);
  Multiplexer #(.select(1), .width(1), .disabled("Z"), .enable("false")) multiplexer_8 (
    .in0(1'b0), .in1(plarom_1_p1[0]), .out(Q1D), .sel(SET));
  Multiplexer #(.select(1), .width(1), .disabled("Z"), .enable("false")) multiplexer_9 (
    .in0(1'b0), .in1(plarom_1_p1[1]), .out(Q1C), .sel(SET));
  Multiplexer #(.select(1), .width(1), .disabled("Z"), .enable("false")) multiplexer_10 (
    .in0(and_24_out), .in1(and_8_out), .out(\Qcc拔 ), .sel(SET));
  and and_24 (and_24_out, not_15_out, and_25_out);
  not not_15 (not_15_out, Adj);
  and and_25 (and_25_out, and_22_out, and_23_out);

  // Notes on the sheet:
  //   ADj时24进制的0封
  //   ADj时12进制的12封
  //   用PLA完成24->12转换
  //   24进制可逆可调计数器部分
  //   这里的12小时的进位由11和计数输入相与产生，能正确产生脉冲信号
  //   12进制与24进制选通部分
endmodule

module \上下午文字显示的电路  (
  input  TT,
  input  AM_FM,
  output [4:0] out_3,
  output [4:0] out_4,
  output [4:0] out_5,
  output [4:0] out_6
);

  wire [4:0] multiplexer_3_out, multiplexer_5_out, multiplexer_6_out, multiplexer_8_out;

  Multiplexer #(.select(1), .width(5), .disabled("Z"), .enable("false")) multiplexer_1 (
    .in0({5{1'b0}}), .in1(multiplexer_5_out), .out(out_3), .sel(TT));
  Multiplexer #(.select(1), .width(5), .disabled("Z"), .enable("false")) multiplexer_2 (
    .in0({5{1'b0}}), .in1(multiplexer_3_out), .out(out_4), .sel(TT));
  Multiplexer #(.select(1), .width(5), .disabled("Z"), .enable("false")) multiplexer_3 (
    .in0(5'b00001), .in1(5'b10000), .out(multiplexer_3_out), .sel(AM_FM));
  Multiplexer #(.select(1), .width(5), .disabled("Z"), .enable("false")) multiplexer_4 (
    .in0({5{1'b0}}), .in1(multiplexer_6_out), .out(out_5), .sel(TT));
  Multiplexer #(.select(1), .width(5), .disabled("Z"), .enable("false")) multiplexer_5 (
    .in0({5{1'b1}}), .in1({5{1'b1}}), .out(multiplexer_5_out), .sel(AM_FM));
  Multiplexer #(.select(1), .width(5), .disabled("Z"), .enable("false")) multiplexer_6 (
    .in0(5'b00101), .in1(5'b10100), .out(multiplexer_6_out), .sel(AM_FM));
  Multiplexer #(.select(1), .width(5), .disabled("Z"), .enable("false")) multiplexer_7 (
    .in0({5{1'b0}}), .in1(multiplexer_8_out), .out(out_6), .sel(TT));
  Multiplexer #(.select(1), .width(5), .disabled("Z"), .enable("false")) multiplexer_8 (
    .in0(5'b00001), .in1(5'b10000), .out(multiplexer_8_out), .sel(AM_FM));
endmodule

module \上下午文字显示测试电路  (
  input  in_1,
  input  in_2
);

  wire [4:0] \上下午文字显示的电路_1_out_3 , \上下午文字显示的电路_1_out_4 , \上下午文字显示的电路_1_out_5 , \上下午文字显示的电路_1_out_6 ;

  DotMatrix #(.inputtype("column"), .matrixcols(4), .matrixrows(5), .persist(0), .dotshape("square")) dotmatrix_1 (
    .col0(\上下午文字显示的电路_1_out_4 ), .col1(\上下午文字显示的电路_1_out_3 ), .col2(\上下午文字显示的电路_1_out_5 ),
    .col3(\上下午文字显示的电路_1_out_6 ));
  \上下午文字显示的电路  \u_上下午文字显示的电路_1  (
    .TT(in_2), .AM_FM(in_1), .out_4(\上下午文字显示的电路_1_out_4 ), .out_3(\上下午文字显示的电路_1_out_3 ),
    .out_5(\上下午文字显示的电路_1_out_5 ), .out_6(\上下午文字显示的电路_1_out_6 ));
endmodule

module \电子钟整点报时电路  (
  input  Clk,
  input  \秒位5D ,
  input  \秒位5A ,
  input  \秒位5C ,
  input  \秒位5B ,
  input  \分位5D ,
  input  \分位5A ,
  input  \分位9D ,
  input  \分位9A ,
  input  \分位5C ,
  input  \分位5B ,
  input  \分位9C ,
  input  \分位9B ,
  output LED
);

  wire and_2_out, and_3_out, and_4_out, and_5_out, and_6_out, and_7_out, and_8_out, and_9_out, and_10_out,
       and_11_out, and_12_out, not_1_out, not_2_out, not_3_out, not_4_out, not_5_out, not_6_out;

  and and_1 (LED, Clk, and_5_out);
  and and_2 (and_2_out, and_3_out, and_4_out);
  and and_3 (and_3_out, not_1_out, \秒位5C );
  not not_1 (not_1_out, \秒位5D );
  and and_4 (and_4_out, not_2_out, \秒位5A );
  not not_2 (not_2_out, \秒位5B );
  and and_5 (and_5_out, and_2_out, and_9_out);
  and and_6 (and_6_out, and_8_out, and_7_out);
  and and_7 (and_7_out, not_4_out, \分位5A );
  and and_8 (and_8_out, not_3_out, \分位5C );
  not not_3 (not_3_out, \分位5D );
  not not_4 (not_4_out, \分位5B );
  and and_9 (and_9_out, and_6_out, and_10_out);
  and and_10 (and_10_out, and_12_out, and_11_out);
  and and_11 (and_11_out, not_5_out, \分位9A );
  and and_12 (and_12_out, \分位9D , not_6_out);
  not not_5 (not_5_out, \分位9B );
  not not_6 (not_6_out, \分位9C );
endmodule

module \电子钟整点报时电路测试电路  (
  input  in_1,
  input  in_2,
  input  in_3,
  input  in_4
);

  wire button_1_out, button_2_out, clock_1_out, \六十进制计数器_1_qcc拔 , \电子钟整点报时电路_1_led , \秒脉冲产生电路_1_out_2 ;
  wire [3:0] \六十进制计数器_1_q0a , \六十进制计数器_1_q1a , \六十进制计数器_2_q0a , \六十进制计数器_2_q1a ;

  Clock #(.highDuration(1), .lowDuration(1)) clock_1 (.out(clock_1_out));
  Hex_Digit_Display hex_digit_display_1 (.value(\六十进制计数器_1_q1a ), .dp(1'b0));
  \秒脉冲产生电路  \u_秒脉冲产生电路_1  (.in_1(clock_1_out), .out_2(\秒脉冲产生电路_1_out_2 ));
  Button button_1 (.out(button_1_out));
  Hex_Digit_Display hex_digit_display_2 (.value(\六十进制计数器_1_q0a ), .dp(1'b0));
  \电子钟整点报时电路  \u_电子钟整点报时电路_1  (
    .LED(\电子钟整点报时电路_1_led ), .\秒位5D (\六十进制计数器_1_q1a [3]), .\秒位5C (\六十进制计数器_1_q1a [2]),
    .\秒位5B (\六十进制计数器_1_q1a [1]), .\秒位5A (\六十进制计数器_1_q1a [0]), .\分位5D (\六十进制计数器_2_q1a [3]),
    .\分位5C (\六十进制计数器_2_q1a [2]), .\分位5B (\六十进制计数器_2_q1a [1]), .\分位5A (\六十进制计数器_2_q1a [0]),
    .\分位9D (\六十进制计数器_2_q0a [3]), .\分位9C (\六十进制计数器_2_q0a [2]), .\分位9B (\六十进制计数器_2_q0a [1]),
    .\分位9A (\六十进制计数器_2_q0a [0]), .Clk(clock_1_out));
  \六十进制计数器  \u_六十进制计数器_1  (
    .Adj(in_1), .Q0D(\六十进制计数器_1_q0a [3]), .Q0C(\六十进制计数器_1_q0a [2]), .Q0B(\六十进制计数器_1_q0a [1]),
    .Q0A(\六十进制计数器_1_q0a [0]), .\Qcc拔 (\六十进制计数器_1_qcc拔 ), .Q1D(\六十进制计数器_1_q1a [3]),
    .out_7(\六十进制计数器_1_q1a [2]), .Q1B(\六十进制计数器_1_q1a [1]), .Q1A(\六十进制计数器_1_q1a [0]), .CLR(in_3),
    .CPu(\秒脉冲产生电路_1_out_2 ), .CPd(button_1_out));
  LED #(.active("true")) led_1 (.in(\电子钟整点报时电路_1_led ));
  Button button_2 (.out(button_2_out));
  Hex_Digit_Display hex_digit_display_3 (.value(\六十进制计数器_2_q1a ), .dp(1'b0));
  Hex_Digit_Display hex_digit_display_4 (.value(\六十进制计数器_2_q0a ), .dp(1'b0));
  \六十进制计数器  \u_六十进制计数器_2  (
    .Adj(in_2), .Q0D(\六十进制计数器_2_q0a [3]), .Q0C(\六十进制计数器_2_q0a [2]), .Q0B(\六十进制计数器_2_q0a [1]),
    .Q0A(\六十进制计数器_2_q0a [0]), .Q1D(\六十进制计数器_2_q1a [3]), .out_7(\六十进制计数器_2_q1a [2]), .Q1B(\六十进制计数器_2_q1a [1]),
    .Q1A(\六十进制计数器_2_q1a [0]), .CLR(in_4), .CPu(\六十进制计数器_1_qcc拔 ), .CPd(button_2_out));  // open: Qcc拔

  // Notes on the sheet:
  //   秒钟
  //   将秒脉冲产生电路整合到该电路中进行测试，建议先调高时钟频率到达59min的测试区间再调低频率进行测试
  //   分钟
endmodule

module \秒脉冲产生电路  (
  input  in_1,
  output out_2
);

  wire and_1_out, and_2_out, and_3_out, buffer_1_out, buffer_2_out, not_1_out, not_2_out, not_3_out,
       or_1_out, \四位二进制可逆计数器_1_out_9 , \四位二进制可逆计数器_1_out_10 , \四位二进制可逆计数器_1_out_11 , \四位二进制可逆计数器_1_out_12 ;

  \四位二进制可逆计数器  \u_四位二进制可逆计数器_1  (
    .D(1'b0), .C(1'b0), .B(1'b0), .A(1'b0), .out_9(\四位二进制可逆计数器_1_out_9 ), .out_10(\四位二进制可逆计数器_1_out_10 ),
    .out_11(\四位二进制可逆计数器_1_out_11 ), .out_12(\四位二进制可逆计数器_1_out_12 ), .\LD拔 (1'b1), .CPu(in_1), .CPd(1'b0),
    .CLR(and_1_out));
  and and_1 (and_1_out, and_3_out, and_2_out);
  and and_2 (and_2_out, not_1_out, not_3_out);
  and and_3 (and_3_out, buffer_1_out, not_2_out);
  not not_1 (not_1_out, \四位二进制可逆计数器_1_out_11 );
  buf buffer_1 (buffer_1_out, \四位二进制可逆计数器_1_out_9 );
  not not_2 (not_2_out, \四位二进制可逆计数器_1_out_10 );
  or or_1 (or_1_out, in_1, buffer_2_out);
  buf buffer_2 (buffer_2_out, and_1_out);
  not not_3 (not_3_out, \四位二进制可逆计数器_1_out_12 );
  J_K_Flip_Flop #(.trigger("rising"), .Pre_Clr_Positions("ABOVE_BELOW"), .NegatePresetClear("false"), .enable("false"), .NewFFLayout("true")) j_k_ff_1 (
    .J(and_1_out), .clk(or_1_out), .K(1'b1), .Q(out_2));  // open: Qn, preset, reset

  // Notes on the sheet:
  //   这个触发器单纯是为了保证脉冲的宽度，根据题意需要可以去除
  //   由于logisimHZ为变化次数，而题意中HZ为脉冲数，因此实际需要将时钟频率调整为16HZ
endmodule

module \多功能数字钟  (
  input  in_1,
  input  in_2,
  input  ADj0,
  input  ADj1,
  input  CLR,
  input  CPu,
  input  CPd,
  input  Set,
  output out_9,
  output [3:0] out_10,
  output [3:0] out_11,
  output [3:0] out_12,
  output [3:0] out_13,
  output [3:0] out_14,
  output [3:0] out_15,
  output [4:0] out_16,
  output [4:0] out_17,
  output [4:0] out_18,
  output [4:0] out_19,
  output out_20
);

  wire and_1_out, and_2_out, and_3_out, and_4_out, and_5_out, and_6_out, and_7_out, d_ff_1_q, d_ff_1_qn,
       not_1_out, not_2_out, not_3_out, or_1_out, or_2_out, or_3_out, or_4_out, or_5_out, \六十进制计数器_1_qcc拔 ,
       \六十进制计数器_2_qcc拔 , \十二进制计数器或二十四进制的计数器电路_1_qcc拔 , \秒脉冲产生电路_1_out_2 ;

  \秒脉冲产生电路  \u_秒脉冲产生电路_1  (.in_1(in_2), .out_2(\秒脉冲产生电路_1_out_2 ));
  \六十进制计数器  \u_六十进制计数器_1  (
    .Adj(1'b0), .Q0D(out_12[3]), .Q0C(out_12[2]), .Q0B(out_12[1]), .Q0A(out_12[0]),
    .\Qcc拔 (\六十进制计数器_1_qcc拔 ), .Q1D(out_11[3]), .out_7(out_11[2]), .Q1B(out_11[1]), .Q1A(out_11[0]),
    .CLR(CLR), .CPu(\秒脉冲产生电路_1_out_2 ), .CPd(1'b0));
  and and_1 (and_1_out, ADj0, not_1_out);
  not not_1 (not_1_out, ADj1);
  and and_2 (and_2_out, CPu, and_1_out);
  or or_1 (or_1_out, and_2_out, \六十进制计数器_1_qcc拔 );
  \闹钟  \u_闹钟_1  (
    .\时1D (out_14[3]), .\时1C (out_14[2]), .\时1B (out_14[1]), .\时1A (out_14[0]), .\时0D (out_15[3]),
    .\时0C (out_15[2]), .\时0B (out_15[1]), .\时0A (out_15[0]), .\分1D (out_13[3]), .\分1C (out_13[2]),
    .\分1B (out_13[1]), .\分1A (out_13[0]), .\分0D (out_10[3]), .\分0C (out_10[2]), .\分0B (out_10[1]),
    .\分0A (out_10[0]), .CLK(\秒脉冲产生电路_1_out_2 ), .LED(out_9), .Alarm(in_1), .Set(Set), .AM_FM(d_ff_1_q),
    .Alramcontrol(1'b1));
  \电子钟整点报时电路  \u_电子钟整点报时电路_1  (
    .LED(out_20), .\秒位5D (out_11[3]), .\秒位5C (out_11[2]), .\秒位5B (out_11[1]), .\秒位5A (out_11[0]),
    .\分位5D (out_13[3]), .\分位5C (out_13[2]), .\分位5B (out_13[1]), .\分位5A (out_13[0]), .\分位9D (out_10[3]),
    .\分位9C (out_10[2]), .\分位9B (out_10[1]), .\分位9A (out_10[0]), .Clk(\秒脉冲产生电路_1_out_2 ));
  \六十进制计数器  \u_六十进制计数器_2  (
    .Adj(and_1_out), .Q0D(out_10[3]), .Q0C(out_10[2]), .Q0B(out_10[1]), .Q0A(out_10[0]),
    .\Qcc拔 (\六十进制计数器_2_qcc拔 ), .Q1D(out_13[3]), .out_7(out_13[2]), .Q1B(out_13[1]), .Q1A(out_13[0]),
    .CLR(CLR), .CPu(or_1_out), .CPd(CPd));
  and and_3 (and_3_out, ADj0, ADj1);
  and and_4 (and_4_out, CPu, and_3_out);
  or or_2 (or_2_out, and_4_out, \六十进制计数器_2_qcc拔 );
  \十二进制计数器或二十四进制的计数器电路  \u_十二进制计数器或二十四进制的计数器电路_1  (
    .SET(Set), .CPu(or_2_out), .CPd(CPd), .Adj(and_3_out), .Q0A(out_15[0]), .Q0B(out_15[1]), .Q0C(out_15[2]),
    .Q0D(out_15[3]), .Q1A(out_14[0]), .Q1B(out_14[1]), .Q1C(out_14[2]), .Q1D(out_14[3]),
    .\Qcc拔 (\十二进制计数器或二十四进制的计数器电路_1_qcc拔 ), .CLR(CLR));
  or or_3 (or_3_out, out_15[3], out_15[2]);
  or or_4 (or_4_out, or_3_out, out_15[1]);
  and and_5 (and_5_out, or_4_out, out_14[0]);
  \上下午文字显示的电路  \u_上下午文字显示的电路_1  (
    .TT(not_2_out), .AM_FM(d_ff_1_q), .out_4(out_16), .out_3(out_17), .out_5(out_18), .out_6(out_19));
  not not_2 (not_2_out, Set);
  and and_6 (and_6_out, or_5_out, Set);
  D_Flip_Flop #(.trigger("rising"), .Pre_Clr_Positions("ABOVE_BELOW"), .NegatePresetClear("false"), .enable("false"), .NewFFLayout("true")) d_ff_1 (
    .clk(\十二进制计数器或二十四进制的计数器电路_1_qcc拔 ), .D(d_ff_1_qn), .Q(d_ff_1_q), .Qn(d_ff_1_qn), .preset(and_6_out),
    .reset(and_7_out));
  and and_7 (and_7_out, not_3_out, Set);
  or or_5 (or_5_out, and_5_out, out_14[1]);
  not not_3 (not_3_out, or_5_out);

  // Notes on the sheet:
  //   同时，用触发器实现它在12小时计数时的正确变化
  //   对上午下午进行补充，使得它在24小时计数时能正确变化AM/PM，准备12小时转换
endmodule

module \多功能数字钟测试电路  (
  input  in_1,
  input  in_2,
  input  in_3,
  input  in_4,
  input  in_5
);

  wire button_1_out, button_2_out, clock_1_out, \多功能数字钟_1_out_9 , \多功能数字钟_1_out_20 ;
  wire [3:0] \多功能数字钟_1_out_10 , \多功能数字钟_1_out_11 , \多功能数字钟_1_out_12 , \多功能数字钟_1_out_13 , \多功能数字钟_1_out_14 ,
       \多功能数字钟_1_out_15 ;
  wire [4:0] \多功能数字钟_1_out_16 , \多功能数字钟_1_out_17 , \多功能数字钟_1_out_18 , \多功能数字钟_1_out_19 ;

  DotMatrix #(.inputtype("column"), .matrixcols(4), .matrixrows(5), .persist(0), .dotshape("square")) dotmatrix_1 (
    .col0(\多功能数字钟_1_out_16 ), .col1(\多功能数字钟_1_out_17 ), .col2(\多功能数字钟_1_out_18 ), .col3(\多功能数字钟_1_out_19 ));
  Clock #(.highDuration(1), .lowDuration(1)) clock_1 (.out(clock_1_out));
  Hex_Digit_Display hex_digit_display_1 (.value(\多功能数字钟_1_out_15 ));  // open: dp
  Hex_Digit_Display hex_digit_display_2 (.value(\多功能数字钟_1_out_14 ));  // open: dp
  \多功能数字钟  \u_多功能数字钟_1  (
    .ADj0(in_1), .ADj1(in_2), .out_20(\多功能数字钟_1_out_20 ), .out_11(\多功能数字钟_1_out_11 ),
    .out_12(\多功能数字钟_1_out_12 ), .out_13(\多功能数字钟_1_out_13 ), .out_10(\多功能数字钟_1_out_10 ),
    .out_14(\多功能数字钟_1_out_14 ), .out_15(\多功能数字钟_1_out_15 ), .CLR(in_5), .CPu(button_2_out),
    .CPd(button_1_out), .Set(in_4), .out_16(\多功能数字钟_1_out_16 ), .out_17(\多功能数字钟_1_out_17 ),
    .out_18(\多功能数字钟_1_out_18 ), .out_19(\多功能数字钟_1_out_19 ), .in_2(clock_1_out), .in_1(in_3),
    .out_9(\多功能数字钟_1_out_9 ));
  Button button_1 (.out(button_1_out));
  Button button_2 (.out(button_2_out));
  Hex_Digit_Display hex_digit_display_3 (.value(\多功能数字钟_1_out_10 ));  // open: dp
  Hex_Digit_Display hex_digit_display_4 (.value(\多功能数字钟_1_out_13 ));  // open: dp
  Hex_Digit_Display hex_digit_display_5 (.value(\多功能数字钟_1_out_11 ));  // open: dp
  Hex_Digit_Display hex_digit_display_6 (.value(\多功能数字钟_1_out_12 ));  // open: dp
  LED #(.active("true")) led_1 (.in(\多功能数字钟_1_out_9 ));
  LED #(.active("true")) led_2 (.in(\多功能数字钟_1_out_20 ));

  // Notes on the sheet:
  //   设定时间后指示灯会闪烁确认
  //   可以将Alarm置为高电平来代替Alarmcontrol停止闹钟
  //   由于题目给定的端口限制，这个电路中Alramcontrol缺省值为1
  //   Alarm的使用：在特定的时间Alarm依次置为高低电平即可设定时间
  //   到达指定的时间（包括12小时制下的AM/FM判定）指示灯会亮起十秒钟
endmodule

module \闹钟  (
  input  \时1D ,
  input  \时1C ,
  input  \时1B ,
  input  \时1A ,
  input  \时0D ,
  input  \时0C ,
  input  Alramcontrol,
  input  \时0B ,
  input  CLK,
  input  \时0A ,
  input  \分1D ,
  input  \分1C ,
  input  \分1B ,
  input  \分1A ,
  input  \分0D ,
  input  \分0C ,
  input  \分0B ,
  input  \分0A ,
  input  AM_FM,
  input  Alarm,
  input  Set,
  output LED
);

  wire and_1_out, and_2_out, and_3_out, and_4_out, and_5_out, and_6_out, and_7_out, and_8_out, and_9_out,
       and_10_out, and_11_out, and_12_out, and_13_out, and_14_out, and_15_out, and_16_out, and_17_out,
       and_18_out, and_19_out, and_20_out, and_21_out, and_22_out, and_23_out, and_24_out, and_25_out,
       and_26_out, and_27_out, and_28_out, and_29_out, and_30_out, and_31_out, and_32_out, and_33_out,
       and_34_out, and_35_out, and_36_out, and_37_out, and_38_out, and_39_out, and_40_out, and_41_out,
       and_42_out, and_43_out, and_44_out, and_45_out, and_46_out, and_47_out, and_48_out, and_49_out,
       and_50_out, and_51_out, and_52_out, and_54_out, and_55_out, and_56_out, comparator_1_eq,
       comparator_2_eq, comparator_3_eq, comparator_4_eq, comparator_5_eq, comparator_6_eq, comparator_7_eq,
       comparator_8_eq, comparator_9_eq, comparator_10_eq, comparator_11_eq, comparator_12_eq,
       comparator_13_eq, comparator_14_eq, comparator_15_eq, comparator_16_eq, comparator_17_eq, d_ff_1_q,
       d_ff_2_q, d_ff_3_q, d_ff_4_q, d_ff_5_q, d_ff_6_q, d_ff_7_q, d_ff_8_q, d_ff_9_q, d_ff_10_q, d_ff_11_q,
       d_ff_12_q, d_ff_13_q, d_ff_14_q, d_ff_15_q, d_ff_16_q, d_ff_17_q, not_1_out, not_2_out, not_3_out,
       not_4_out, not_5_out, not_6_out, not_7_out, not_8_out, not_9_out, not_10_out, not_11_out, not_12_out,
       not_13_out, not_14_out, not_15_out, not_16_out, not_17_out, not_18_out, not_19_out, not_20_out,
       not_21_out, or_1_out, or_2_out, \四位二进制可逆计数器_1_out_9 , \四位二进制可逆计数器_1_out_11 ;

  not not_1 (not_1_out, \时1D );
  not not_2 (not_2_out, \时1C );
  not not_3 (not_3_out, \时1B );
  not not_4 (not_4_out, \时1A );
  not not_5 (not_5_out, \时0D );
  not not_6 (not_6_out, \时0C );
  not not_7 (not_7_out, \时0B );
  not not_8 (not_8_out, \时0A );
  not not_9 (not_9_out, \分1D );
  not not_10 (not_10_out, \分1C );
  not not_11 (not_11_out, \分1B );
  not not_12 (not_12_out, \分1A );
  not not_13 (not_13_out, \分0D );
  not not_14 (not_14_out, \分0C );
  not not_15 (not_15_out, \分0B );
  not not_16 (not_16_out, \分0A );
  not not_17 (not_17_out, AM_FM);
  and and_1 (and_1_out, \时1D , Alarm);
  and and_2 (and_2_out, not_1_out, Alarm);
  and and_3 (and_3_out, \时1C , Alarm);
  and and_4 (and_4_out, not_2_out, Alarm);
  and and_5 (and_5_out, \时1B , Alarm);
  and and_6 (and_6_out, not_3_out, Alarm);
  and and_7 (and_7_out, \时1A , Alarm);
  and and_8 (and_8_out, not_4_out, Alarm);
  and and_9 (and_9_out, \时0D , Alarm);
  and and_10 (and_10_out, not_5_out, Alarm);
  and and_11 (and_11_out, \时0C , Alarm);
  and and_12 (and_12_out, not_6_out, Alarm);
  and and_13 (and_13_out, \时0B , Alarm);
  and and_14 (and_14_out, not_7_out, Alarm);
  and and_15 (and_15_out, \时0A , Alarm);
  and and_16 (and_16_out, not_8_out, Alarm);
  and and_17 (and_17_out, \分1D , Alarm);
  and and_18 (and_18_out, not_9_out, Alarm);
  and and_19 (and_19_out, \分1C , Alarm);
  and and_20 (and_20_out, not_10_out, Alarm);
  and and_21 (and_21_out, \分1B , Alarm);
  and and_22 (and_22_out, not_11_out, Alarm);
  and and_23 (and_23_out, \分1A , Alarm);
  and and_24 (and_24_out, not_12_out, Alarm);
  and and_25 (and_25_out, \分0D , Alarm);
  and and_26 (and_26_out, not_13_out, Alarm);
  and and_27 (and_27_out, \分0C , Alarm);
  and and_28 (and_28_out, not_14_out, Alarm);
  and and_29 (and_29_out, \分0B , Alarm);
  and and_30 (and_30_out, not_15_out, Alarm);
  and and_31 (and_31_out, \分0A , Alarm);
  and and_32 (and_32_out, not_16_out, Alarm);
  and and_33 (and_33_out, AM_FM, Alarm);
  and and_34 (and_34_out, not_17_out, Alarm);
  D_Flip_Flop #(.trigger("falling"), .Pre_Clr_Positions("ABOVE_BELOW"), .NegatePresetClear("false"), .enable("false"), .NewFFLayout("true")) d_ff_1 (
    .clk(1'b1), .Q(d_ff_1_q), .preset(and_1_out), .reset(and_2_out));  // open: D, Qn
  D_Flip_Flop #(.trigger("falling"), .Pre_Clr_Positions("ABOVE_BELOW"), .NegatePresetClear("false"), .enable("false"), .NewFFLayout("true")) d_ff_2 (
    .clk(1'b1), .Q(d_ff_2_q), .preset(and_3_out), .reset(and_4_out));  // open: D, Qn
  D_Flip_Flop #(.trigger("falling"), .Pre_Clr_Positions("ABOVE_BELOW"), .NegatePresetClear("false"), .enable("false"), .NewFFLayout("true")) d_ff_3 (
    .clk(1'b1), .Q(d_ff_3_q), .preset(and_5_out), .reset(and_6_out));  // open: D, Qn
  D_Flip_Flop #(.trigger("falling"), .Pre_Clr_Positions("ABOVE_BELOW"), .NegatePresetClear("false"), .enable("false"), .NewFFLayout("true")) d_ff_4 (
    .clk(1'b1), .Q(d_ff_4_q), .preset(and_7_out), .reset(and_8_out));  // open: D, Qn
  D_Flip_Flop #(.trigger("falling"), .Pre_Clr_Positions("ABOVE_BELOW"), .NegatePresetClear("false"), .enable("false"), .NewFFLayout("true")) d_ff_5 (
    .clk(1'b1), .Q(d_ff_5_q), .preset(and_9_out), .reset(and_10_out));  // open: D, Qn
  D_Flip_Flop #(.trigger("falling"), .Pre_Clr_Positions("ABOVE_BELOW"), .NegatePresetClear("false"), .enable("false"), .NewFFLayout("true")) d_ff_6 (
    .clk(1'b1), .Q(d_ff_6_q), .preset(and_11_out), .reset(and_12_out));  // open: D, Qn
  D_Flip_Flop #(.trigger("falling"), .Pre_Clr_Positions("ABOVE_BELOW"), .NegatePresetClear("false"), .enable("false"), .NewFFLayout("true")) d_ff_7 (
    .clk(1'b1), .Q(d_ff_7_q), .preset(and_13_out), .reset(and_14_out));  // open: D, Qn
  D_Flip_Flop #(.trigger("falling"), .Pre_Clr_Positions("ABOVE_BELOW"), .NegatePresetClear("false"), .enable("false"), .NewFFLayout("true")) d_ff_8 (
    .clk(1'b1), .Q(d_ff_8_q), .preset(and_15_out), .reset(and_16_out));  // open: D, Qn
  D_Flip_Flop #(.trigger("falling"), .Pre_Clr_Positions("ABOVE_BELOW"), .NegatePresetClear("false"), .enable("false"), .NewFFLayout("true")) d_ff_9 (
    .clk(1'b1), .Q(d_ff_9_q), .preset(and_17_out), .reset(and_18_out));  // open: D, Qn
  D_Flip_Flop #(.trigger("falling"), .Pre_Clr_Positions("ABOVE_BELOW"), .NegatePresetClear("false"), .enable("false"), .NewFFLayout("true")) d_ff_10 (
    .clk(1'b1), .Q(d_ff_10_q), .preset(and_19_out), .reset(and_20_out));  // open: D, Qn
  D_Flip_Flop #(.trigger("falling"), .Pre_Clr_Positions("ABOVE_BELOW"), .NegatePresetClear("false"), .enable("false"), .NewFFLayout("true")) d_ff_11 (
    .clk(1'b1), .Q(d_ff_11_q), .preset(and_21_out), .reset(and_22_out));  // open: D, Qn
  D_Flip_Flop #(.trigger("falling"), .Pre_Clr_Positions("ABOVE_BELOW"), .NegatePresetClear("false"), .enable("false"), .NewFFLayout("true")) d_ff_12 (
    .clk(1'b1), .Q(d_ff_12_q), .preset(and_23_out), .reset(and_24_out));  // open: D, Qn
  D_Flip_Flop #(.trigger("falling"), .Pre_Clr_Positions("ABOVE_BELOW"), .NegatePresetClear("false"), .enable("false"), .NewFFLayout("true")) d_ff_13 (
    .clk(1'b1), .Q(d_ff_13_q), .preset(and_25_out), .reset(and_26_out));  // open: D, Qn
  D_Flip_Flop #(.trigger("falling"), .Pre_Clr_Positions("ABOVE_BELOW"), .NegatePresetClear("false"), .enable("false"), .NewFFLayout("true")) d_ff_14 (
    .clk(1'b1), .Q(d_ff_14_q), .preset(and_27_out), .reset(and_28_out));  // open: D, Qn
  D_Flip_Flop #(.trigger("falling"), .Pre_Clr_Positions("ABOVE_BELOW"), .NegatePresetClear("false"), .enable("false"), .NewFFLayout("true")) d_ff_15 (
    .clk(1'b1), .Q(d_ff_15_q), .preset(and_29_out), .reset(and_30_out));  // open: D, Qn
  D_Flip_Flop #(.trigger("falling"), .Pre_Clr_Positions("ABOVE_BELOW"), .NegatePresetClear("false"), .enable("false"), .NewFFLayout("true")) d_ff_16 (
    .clk(1'b1), .Q(d_ff_16_q), .preset(and_31_out), .reset(and_32_out));  // open: D, Qn
  D_Flip_Flop #(.trigger("falling"), .Pre_Clr_Positions("ABOVE_BELOW"), .NegatePresetClear("false"), .enable("false"), .NewFFLayout("true")) d_ff_17 (
    .clk(1'b1), .Q(d_ff_17_q), .preset(and_33_out), .reset(and_34_out));  // open: D, Qn
  Comparator #(.width(1), .mode("twosComplement")) comparator_1 (
    .a(\时1D ), .b(d_ff_1_q), .eq(comparator_1_eq));  // open: gt, lt
  Comparator #(.width(1), .mode("twosComplement")) comparator_2 (
    .a(\时1C ), .b(d_ff_2_q), .eq(comparator_2_eq));  // open: gt, lt
  Comparator #(.width(1), .mode("twosComplement")) comparator_3 (
    .a(\时1B ), .b(d_ff_3_q), .eq(comparator_3_eq));  // open: gt, lt
  Comparator #(.width(1), .mode("twosComplement")) comparator_4 (
    .a(\时1A ), .b(d_ff_4_q), .eq(comparator_4_eq));  // open: gt, lt
  Comparator #(.width(1), .mode("twosComplement")) comparator_5 (
    .a(\时0D ), .b(d_ff_5_q), .eq(comparator_5_eq));  // open: gt, lt
  Comparator #(.width(1), .mode("twosComplement")) comparator_6 (
    .a(\时0C ), .b(d_ff_6_q), .eq(comparator_6_eq));  // open: gt, lt
  Comparator #(.width(1), .mode("twosComplement")) comparator_7 (
    .a(\时0B ), .b(d_ff_7_q), .eq(comparator_7_eq));  // open: gt, lt
  Comparator #(.width(1), .mode("twosComplement")) comparator_8 (
    .a(\时0A ), .b(d_ff_8_q), .eq(comparator_8_eq));  // open: gt, lt
  Comparator #(.width(1), .mode("twosComplement")) comparator_9 (
    .a(\分1D ), .b(d_ff_9_q), .eq(comparator_9_eq));  // open: gt, lt
  Comparator #(.width(1), .mode("twosComplement")) comparator_10 (
    .a(\分1C ), .b(d_ff_10_q), .eq(comparator_10_eq));  // open: gt, lt
  Comparator #(.width(1), .mode("twosComplement")) comparator_11 (
    .a(\分1B ), .b(d_ff_11_q), .eq(comparator_11_eq));  // open: gt, lt
  Comparator #(.width(1), .mode("twosComplement")) comparator_12 (
    .a(\分1A ), .b(d_ff_12_q), .eq(comparator_12_eq));  // open: gt, lt
  Comparator #(.width(1), .mode("twosComplement")) comparator_13 (
    .a(\分0D ), .b(d_ff_13_q), .eq(comparator_13_eq));  // open: gt, lt
  Comparator #(.width(1), .mode("twosComplement")) comparator_14 (
    .a(\分0C ), .b(d_ff_14_q), .eq(comparator_14_eq));  // open: gt, lt
  Comparator #(.width(1), .mode("twosComplement")) comparator_15 (
    .a(\分0B ), .b(d_ff_15_q), .eq(comparator_15_eq));  // open: gt, lt
  Comparator #(.width(1), .mode("twosComplement")) comparator_16 (
    .a(\分0A ), .b(d_ff_16_q), .eq(comparator_16_eq));  // open: gt, lt
  Comparator #(.width(1), .mode("twosComplement")) comparator_17 (
    .a(AM_FM), .b(d_ff_17_q), .eq(comparator_17_eq));  // open: gt, lt
  and and_35 (and_35_out, comparator_1_eq, comparator_2_eq);
  and and_36 (and_36_out, comparator_3_eq, comparator_4_eq);
  and and_37 (and_37_out, comparator_5_eq, comparator_6_eq);
  and and_38 (and_38_out, comparator_7_eq, comparator_8_eq);
  and and_39 (and_39_out, comparator_9_eq, comparator_10_eq);
  and and_40 (and_40_out, comparator_11_eq, comparator_12_eq);
  and and_41 (and_41_out, comparator_13_eq, comparator_14_eq);
  and and_42 (and_42_out, comparator_15_eq, comparator_16_eq);
  not not_18 (not_18_out, Set);
  and and_43 (and_43_out, and_35_out, and_36_out);
  and and_44 (and_44_out, and_37_out, and_38_out);
  and and_45 (and_45_out, and_39_out, and_40_out);
  and and_46 (and_46_out, and_41_out, and_42_out);
  and and_47 (and_47_out, comparator_17_eq, not_18_out);
  and and_48 (and_48_out, and_43_out, and_44_out);
  and and_49 (and_49_out, and_48_out, and_50_out);
  and and_50 (and_50_out, and_45_out, and_46_out);
  or or_1 (or_1_out, and_47_out, Set);
  and and_51 (and_51_out, and_49_out, or_1_out);
  not not_19 (not_19_out, and_51_out);
  or or_2 (or_2_out, not_19_out, Alarm);
  and and_52 (and_52_out, CLK, not_21_out);
  and and_53 (LED, CLK, and_54_out);
  and and_54 (and_54_out, and_55_out, Alramcontrol);
  and and_55 (and_55_out, not_20_out, not_21_out);
  not not_20 (not_20_out, or_2_out);
  not not_21 (not_21_out, and_56_out);
  and and_56 (and_56_out, \四位二进制可逆计数器_1_out_9 , \四位二进制可逆计数器_1_out_11 );
  \四位二进制可逆计数器  \u_四位二进制可逆计数器_1  (
    .D(1'b0), .C(1'b0), .B(1'b0), .A(1'b0), .out_9(\四位二进制可逆计数器_1_out_9 ), .out_11(\四位二进制可逆计数器_1_out_11 ),
    .\LD拔 (1'b1), .CPu(and_52_out), .CPd(1'b0), .CLR(or_2_out));  // open: out_10, out_12

  // Notes on the sheet:
  //   闹钟考虑了12/24小时两种时间制
endmodule

module \闹钟测试  (
  input  in_1,
  input  in_2,
  input  in_3,
  input  in_4,
  input  in_5,
  input  in_6,
  input  in_7,
  input  in_8,
  input  in_9
);

  wire clock_1_out, clock_2_out, \六十进制计数器_1_qcc拔 , \六十进制计数器_2_qcc拔 , \闹钟_1_led ;
  wire [3:0] \六十进制计数器_2_q0a , \六十进制计数器_2_q1a , \十二进制计数器或二十四进制的计数器电路_1_q0a , \十二进制计数器或二十四进制的计数器电路_1_q1a ;

  Hex_Digit_Display hex_digit_display_1 (.value(\六十进制计数器_2_q1a ));  // open: dp
  Clock #(.highDuration(1), .lowDuration(1)) clock_1 (.out(clock_1_out));
  Hex_Digit_Display hex_digit_display_2 (.value(\六十进制计数器_2_q0a ));  // open: dp
  Clock #(.highDuration(1), .lowDuration(1)) clock_2 (.out(clock_2_out));
  \六十进制计数器  \u_六十进制计数器_1  (
    .Adj(in_6), .\Qcc拔 (\六十进制计数器_1_qcc拔 ), .CLR(in_9), .CPu(clock_1_out), .CPd(in_8));  // open: Q0D, Q0C, Q0B, Q0A, Q1D, out_7, Q1B, Q1A
  \六十进制计数器  \u_六十进制计数器_2  (
    .Adj(in_7), .Q0D(\六十进制计数器_2_q0a [3]), .Q0C(\六十进制计数器_2_q0a [2]), .Q0B(\六十进制计数器_2_q0a [1]),
    .Q0A(\六十进制计数器_2_q0a [0]), .\Qcc拔 (\六十进制计数器_2_qcc拔 ), .Q1D(\六十进制计数器_2_q1a [3]),
    .out_7(\六十进制计数器_2_q1a [2]), .Q1B(\六十进制计数器_2_q1a [1]), .Q1A(\六十进制计数器_2_q1a [0]), .CLR(in_9),
    .CPu(\六十进制计数器_1_qcc拔 ), .CPd(1'b0));
  Hex_Digit_Display hex_digit_display_3 (.value(\十二进制计数器或二十四进制的计数器电路_1_q1a ));  // open: dp
  \闹钟  \u_闹钟_1  (
    .\时1D (\十二进制计数器或二十四进制的计数器电路_1_q1a [3]), .\时1C (\十二进制计数器或二十四进制的计数器电路_1_q1a [2]),
    .\时1B (\十二进制计数器或二十四进制的计数器电路_1_q1a [1]), .\时1A (\十二进制计数器或二十四进制的计数器电路_1_q1a [0]),
    .\时0D (\十二进制计数器或二十四进制的计数器电路_1_q0a [3]), .\时0C (\十二进制计数器或二十四进制的计数器电路_1_q0a [2]),
    .\时0B (\十二进制计数器或二十四进制的计数器电路_1_q0a [1]), .\时0A (\十二进制计数器或二十四进制的计数器电路_1_q0a [0]),
    .\分1D (\六十进制计数器_2_q1a [3]), .\分1C (\六十进制计数器_2_q1a [2]), .\分1B (\六十进制计数器_2_q1a [1]),
    .\分1A (\六十进制计数器_2_q1a [0]), .\分0D (\六十进制计数器_2_q0a [3]), .\分0C (\六十进制计数器_2_q0a [2]),
    .\分0B (\六十进制计数器_2_q0a [1]), .\分0A (\六十进制计数器_2_q0a [0]), .CLK(clock_2_out), .LED(\闹钟_1_led ),
    .Alarm(in_2), .Set(in_5), .AM_FM(in_3), .Alramcontrol(in_1));
  Hex_Digit_Display hex_digit_display_4 (.value(\十二进制计数器或二十四进制的计数器电路_1_q0a ));  // open: dp
  LED #(.active("true")) led_1 (.in(\闹钟_1_led ));
  \十二进制计数器或二十四进制的计数器电路  \u_十二进制计数器或二十四进制的计数器电路_1  (
    .SET(in_5), .CPu(\六十进制计数器_2_qcc拔 ), .CPd(1'b0), .Adj(in_4), .Q0A(\十二进制计数器或二十四进制的计数器电路_1_q0a [0]),
    .Q0B(\十二进制计数器或二十四进制的计数器电路_1_q0a [1]), .Q0C(\十二进制计数器或二十四进制的计数器电路_1_q0a [2]),
    .Q0D(\十二进制计数器或二十四进制的计数器电路_1_q0a [3]), .Q1A(\十二进制计数器或二十四进制的计数器电路_1_q1a [0]),
    .Q1B(\十二进制计数器或二十四进制的计数器电路_1_q1a [1]), .Q1C(\十二进制计数器或二十四进制的计数器电路_1_q1a [2]),
    .Q1D(\十二进制计数器或二十四进制的计数器电路_1_q1a [3]), .CLR(in_9));  // open: Qcc拔

  // Notes on the sheet:
  //   分钟
  //   此处AM/FM需要手动设置，建议直接使用多功能数字钟测试电路
  //   小时
endmodule
