// Logisim project 实验6-ACM1801-U201814565-王家璇.circ as structural Verilog: 8 circuits, main circuit sqrX
module sqrX (
  input  [31:0] in_1,
  input  [31:0] in_2,
  input  [31:0] in_3,
  input  [31:0] in_4,
  output [31:0] a_prime,
  output [31:0] b_prime,
  output [31:0] c_prime,
  output [31:0] d_prime
);

  wire [31:0] multiplier_1_out, multiplier_2_out, multiplier_3_out, multiplier_4_out, multiplier_5_out,
       multiplier_6_out, multiplier_7_out;

  Multiplier #(.width(32)) multiplier_1 (.a(in_1), .b(in_1), .out(multiplier_1_out), .cin({32{1'b0}}));  // open: cout
  Multiplier #(.width(32)) multiplier_2 (.a(in_1), .b(in_2), .out(multiplier_2_out), .cin({32{1'b0}}));  // open: cout
  Multiplier #(.width(32)) multiplier_3 (.a(in_2), .b(in_3), .out(multiplier_3_out), .cin({32{1'b0}}));  // open: cout
  Multiplier #(.width(32)) multiplier_4 (.a(in_2), .b(in_4), .out(multiplier_4_out), .cin({32{1'b0}}));  // open: cout
  Multiplier #(.width(32)) multiplier_5 (.a(in_3), .b(in_1), .out(multiplier_5_out), .cin({32{1'b0}}));  // open: cout
  Multiplier #(.width(32)) multiplier_6 (.a(in_3), .b(in_4), .out(multiplier_6_out), .cin({32{1'b0}}));  // open: cout
  Multiplier #(.width(32)) multiplier_7 (.a(in_4), .b(in_4), .out(multiplier_7_out), .cin({32{1'b0}}));  // open: cout
  Adder #(.width(32)) adder_1 (.a(multiplier_1_out), .b(multiplier_3_out), .out(a_prime), .cin(1'b0));  // open: cout
  Adder #(.width(32)) adder_2 (.a(multiplier_2_out), .b(multiplier_4_out), .out(b_prime), .cin(1'b0));  // open: cout
  Adder #(.width(32)) adder_3 (.a(multiplier_5_out), .b(multiplier_6_out), .out(c_prime), .cin(1'b0));  // open: cout
  Adder #(.width(32)) adder_4 (.a(multiplier_3_out), .b(multiplier_7_out), .out(d_prime), .cin(1'b0));  // open: cout
endmodule

module sqrX_A (
  input  [31:0] in_1,
  input  [31:0] in_2,
  input  [31:0] in_3,
  input  [31:0] in_4,
  output [31:0] a_prime,
  output [31:0] b_prime,
  output [31:0] c_prime,
  output [31:0] d_prime
);

  wire [31:0] adder_2_out, adder_4_out, multiplier_1_out, multiplier_2_out, multiplier_3_out,
       multiplier_4_out, multiplier_5_out, multiplier_6_out, multiplier_7_out;

  Multiplier #(.width(32)) multiplier_1 (.a(in_1), .b(in_1), .out(multiplier_1_out), .cin({32{1'b0}}));  // open: cout
  Multiplier #(.width(32)) multiplier_2 (.a(in_1), .b(in_2), .out(multiplier_2_out), .cin({32{1'b0}}));  // open: cout
  Multiplier #(.width(32)) multiplier_3 (.a(in_2), .b(in_3), .out(multiplier_3_out), .cin({32{1'b0}}));  // open: cout
  Multiplier #(.width(32)) multiplier_4 (.a(in_2), .b(in_4), .out(multiplier_4_out), .cin({32{1'b0}}));  // open: cout
  Multiplier #(.width(32)) multiplier_5 (.a(in_3), .b(in_1), .out(multiplier_5_out), .cin({32{1'b0}}));  // open: cout
  Multiplier #(.width(32)) multiplier_6 (.a(in_3), .b(in_4), .out(multiplier_6_out), .cin({32{1'b0}}));  // open: cout
  Multiplier #(.width(32)) multiplier_7 (.a(in_4), .b(in_4), .out(multiplier_7_out), .cin({32{1'b0}}));  // open: cout
  Adder #(.width(32)) adder_1 (.a(multiplier_2_out), .b(multiplier_4_out), .out(a_prime), .cin(1'b0));  // open: cout
  Adder #(.width(32)) adder_2 (
    .a(multiplier_1_out), .b(multiplier_3_out), .out(adder_2_out), .cin(1'b0));  // open: cout
  Adder #(.width(32)) adder_3 (.a(multiplier_3_out), .b(multiplier_7_out), .out(c_prime), .cin(1'b0));  // open: cout
  Adder #(.width(32)) adder_4 (
    .a(multiplier_5_out), .b(multiplier_6_out), .out(adder_4_out), .cin(1'b0));  // open: cout
  Adder #(.width(32)) adder_5 (.a(a_prime), .b(adder_2_out), .out(b_prime), .cin(1'b0));  // open: cout
  Adder #(.width(32)) adder_6 (.a(c_prime), .b(adder_4_out), .out(d_prime), .cin(1'b0));  // open: cout
endmodule

module \Fibonacci数显示模块  (
  input  [31:0] in_1,
  output [3:0] D0,
  output [3:0] D1,
  output [3:0] D2,
  output [3:0] D3,
  output [3:0] D4,
  output [3:0] D5,
  output [3:0] D6,
  output [3:0] D7,
  output [3:0] D8,
  output [3:0] D9
);

  wire [31:0] divider_1_out, divider_2_out, divider_3_out, divider_4_out, divider_5_out, divider_7_out,
       divider_8_out, divider_9_out, divider_10_out;
  wire [31:4] divider_1_rem, divider_2_rem, divider_3_rem, divider_4_rem, divider_5_rem, divider_6_rem,
       divider_7_rem, divider_8_rem, divider_9_rem, divider_10_rem;

  Divider #(.width(32)) divider_1 (
    .a(in_1), .b(32'ha), .out(divider_1_out), .upper({32{1'b0}}), .rem({divider_1_rem, D0}));
  Divider #(.width(32)) divider_2 (
    .a(divider_9_out), .b(32'ha), .out(divider_2_out), .upper({32{1'b0}}), .rem({divider_2_rem, D4}));
  Divider #(.width(32)) divider_3 (
    .a(divider_10_out), .b(32'ha), .out(divider_3_out), .upper({32{1'b0}}), .rem({divider_3_rem, D8}));
  Divider #(.width(32)) divider_4 (
    .a(divider_1_out), .b(32'ha), .out(divider_4_out), .upper({32{1'b0}}), .rem({divider_4_rem, D1}));
  Divider #(.width(32)) divider_5 (
    .a(divider_2_out), .b(32'ha), .out(divider_5_out), .upper({32{1'b0}}), .rem({divider_5_rem, D5}));
  Divider #(.width(32)) divider_6 (
    .a(divider_3_out), .b(32'ha), .upper({32{1'b0}}), .rem({divider_6_rem, D9}));  // open: out
  Divider #(.width(32)) divider_7 (
    .a(divider_4_out), .b(32'ha), .out(divider_7_out), .upper({32{1'b0}}), .rem({divider_7_rem, D2}));
  Divider #(.width(32)) divider_8 (
    .a(divider_5_out), .b(32'ha), .out(divider_8_out), .upper({32{1'b0}}), .rem({divider_8_rem, D6}));
  Divider #(.width(32)) divider_9 (
    .a(divider_7_out), .b(32'ha), .out(divider_9_out), .upper({32{1'b0}}), .rem({divider_9_rem, D3}));
  Divider #(.width(32)) divider_10 (
    .a(divider_8_out), .b(32'ha), .out(divider_10_out), .upper({32{1'b0}}), .rem({divider_10_rem, D7}));
endmodule

module \斐波那契_Fibonacci_数列计算器  (
  input  [5:0] in_1,
  input  in_2,
  input  in_3,
  output [3:0] out_4,
  output [3:0] out_5,
  output [3:0] out_6,
  output [3:0] out_7,
  output [3:0] out_8,
  output [3:0] out_9,
  output [3:0] out_10,
  output [3:0] out_11,
  output [3:0] out_12,
  output [3:0] out_13
);

  wire \控制器_1_clear_2 , \控制器_1_clk , \控制器_1_ni_1 , \控制器_1_start ;
  wire [31:0] \矩阵快速幂算法迭代模块_1_fi ;

  \控制器  \u_控制器_1  (
    .clear(in_2), .ni_1(\控制器_1_ni_1 ), .start(\控制器_1_start ), .clk(\控制器_1_clk ), .clear_2(\控制器_1_clear_2 ),
    .n(in_1), .clock(in_3));
  \矩阵快速幂算法迭代模块  \u_矩阵快速幂算法迭代模块_1  (
    .Start(\控制器_1_start ), .clk(\控制器_1_clk ), .clr(\控制器_1_clear_2 ), .Fi(\矩阵快速幂算法迭代模块_1_fi ),
    .ni_1(\控制器_1_ni_1 ));
  \Fibonacci数显示模块  \fibonacci数显示模块_1  (
    .in_1(\矩阵快速幂算法迭代模块_1_fi ), .D0(out_13), .D4(out_9), .D1(out_12), .D5(out_8), .D2(out_11), .D6(out_7),
    .D3(out_10), .D7(out_6), .D8(out_5), .D9(out_4));
endmodule

module \斐波那契_Fibonacci_数列计算器验证电路  (
  input  [5:0] in_1
);

  wire button_1_out, button_2_out;
  wire [3:0] \斐波那契_fibonacci_数列计算器_1_out_4 , \斐波那契_fibonacci_数列计算器_1_out_5 , \斐波那契_fibonacci_数列计算器_1_out_6 ,
       \斐波那契_fibonacci_数列计算器_1_out_7 , \斐波那契_fibonacci_数列计算器_1_out_8 , \斐波那契_fibonacci_数列计算器_1_out_9 ,
       \斐波那契_fibonacci_数列计算器_1_out_10 , \斐波那契_fibonacci_数列计算器_1_out_11 , \斐波那契_fibonacci_数列计算器_1_out_12 ,
       \斐波那契_fibonacci_数列计算器_1_out_13 ;

  Button button_1 (.out(button_1_out));
  Button button_2 (.out(button_2_out));
  \斐波那契_Fibonacci_数列计算器  \u_斐波那契_fibonacci_数列计算器_1  (
    .in_1(in_1), .in_2(button_1_out), .in_3(button_2_out), .out_4(\斐波那契_fibonacci_数列计算器_1_out_4 ),
    .out_5(\斐波那契_fibonacci_数列计算器_1_out_5 ), .out_7(\斐波那契_fibonacci_数列计算器_1_out_7 ),
    .out_6(\斐波那契_fibonacci_数列计算器_1_out_6 ), .out_8(\斐波那契_fibonacci_数列计算器_1_out_8 ),
    .out_9(\斐波那契_fibonacci_数列计算器_1_out_9 ), .out_10(\斐波那契_fibonacci_数列计算器_1_out_10 ),
    .out_11(\斐波那契_fibonacci_数列计算器_1_out_11 ), .out_12(\斐波那契_fibonacci_数列计算器_1_out_12 ),
    .out_13(\斐波那契_fibonacci_数列计算器_1_out_13 ));
  Hex_Digit_Display hex_digit_display_1 (.value(\斐波那契_fibonacci_数列计算器_1_out_4 ));  // open: dp
  Hex_Digit_Display hex_digit_display_2 (.value(\斐波那契_fibonacci_数列计算器_1_out_5 ));  // open: dp
  Hex_Digit_Display hex_digit_display_3 (.value(\斐波那契_fibonacci_数列计算器_1_out_6 ));  // open: dp
  Hex_Digit_Display hex_digit_display_4 (.value(\斐波那契_fibonacci_数列计算器_1_out_7 ));  // open: dp
  Hex_Digit_Display hex_digit_display_5 (.value(\斐波那契_fibonacci_数列计算器_1_out_8 ));  // open: dp
  Hex_Digit_Display hex_digit_display_6 (.value(\斐波那契_fibonacci_数列计算器_1_out_9 ));  // open: dp
  Hex_Digit_Display hex_digit_display_7 (.value(\斐波那契_fibonacci_数列计算器_1_out_10 ));  // open: dp
  Hex_Digit_Display hex_digit_display_8 (.value(\斐波那契_fibonacci_数列计算器_1_out_11 ));  // open: dp
  Hex_Digit_Display hex_digit_display_9 (.value(\斐波那契_fibonacci_数列计算器_1_out_12 ));  // open: dp
  Hex_Digit_Display hex_digit_display_10 (.value(\斐波那契_fibonacci_数列计算器_1_out_13 ));  // open: dp
endmodule

module \矩阵快速幂算法迭代模块  (
  input  Start,
  input  clk,
  input  clr,
  input  ni_1,
  output [31:0] Fi
);

  wire [31:0] multiplexer_1_out, multiplexer_2_out, multiplexer_3_out, multiplexer_4_out, multiplexer_5_out,
       multiplexer_6_out, multiplexer_7_out, multiplexer_8_out, register_1_q, register_3_q, register_4_q,
       sqrx_1_a_prime, sqrx_1_b_prime, sqrx_1_c_prime, sqrx_1_d_prime, sqrx_a_1_a_prime, sqrx_a_1_b_prime,
       sqrx_a_1_c_prime, sqrx_a_1_d_prime;

  Multiplexer #(.select(1), .width(32), .disabled("Z"), .enable("false")) multiplexer_1 (
    .in0({32{1'b0}}), .in1(multiplexer_5_out), .out(multiplexer_1_out), .sel(Start));
  Register #(.width(32), .trigger("rising"), .Select("low")) register_1 (
    .D(multiplexer_1_out), .en(1'b1), .Q(register_1_q), .clk(clk), .clr(clr), .cs(1'b0), .preset(1'b0));
  Multiplexer #(.select(1), .width(32), .disabled("Z"), .enable("false")) multiplexer_2 (
    .in0(32'h1), .in1(multiplexer_6_out), .out(multiplexer_2_out), .sel(Start));
  Register #(.width(32), .trigger("rising"), .Select("low")) register_2 (
    .D(multiplexer_2_out), .en(1'b1), .Q(Fi), .clk(clk), .clr(clr), .cs(1'b0), .preset(1'b0));
  Multiplexer #(.select(1), .width(32), .disabled("Z"), .enable("false")) multiplexer_3 (
    .in0(32'h1), .in1(multiplexer_7_out), .out(multiplexer_3_out), .sel(Start));
  Register #(.width(32), .trigger("rising"), .Select("low")) register_3 (
    .D(multiplexer_3_out), .en(1'b1), .Q(register_3_q), .clk(clk), .clr(clr), .cs(1'b0), .preset(1'b0));
  Multiplexer #(.select(1), .width(32), .disabled("Z"), .enable("false")) multiplexer_4 (
    .in0(32'h1), .in1(multiplexer_8_out), .out(multiplexer_4_out), .sel(Start));
  Register #(.width(32), .trigger("rising"), .Select("low")) register_4 (
    .D(multiplexer_4_out), .en(1'b1), .Q(register_4_q), .clk(clk), .clr(clr), .cs(1'b0), .preset(1'b0));
  sqrX sqrx_1 (
    .in_1(register_1_q), .in_2(Fi), .in_3(register_3_q), .in_4(register_4_q), .a_prime(sqrx_1_a_prime),
    .b_prime(sqrx_1_b_prime), .c_prime(sqrx_1_c_prime), .d_prime(sqrx_1_d_prime));
  sqrX_A sqrx_a_1 (
    .in_1(register_1_q), .in_2(Fi), .in_3(register_3_q), .in_4(register_4_q), .a_prime(sqrx_a_1_a_prime),
    .b_prime(sqrx_a_1_b_prime), .c_prime(sqrx_a_1_c_prime), .d_prime(sqrx_a_1_d_prime));
  Multiplexer #(.select(1), .width(32), .disabled("Z"), .enable("false")) multiplexer_5 (
    .in0(sqrx_1_a_prime), .in1(sqrx_a_1_a_prime), .out(multiplexer_5_out), .sel(ni_1));
  Multiplexer #(.select(1), .width(32), .disabled("Z"), .enable("false")) multiplexer_6 (
    .in0(sqrx_1_b_prime), .in1(sqrx_a_1_b_prime), .out(multiplexer_6_out), .sel(ni_1));
  Multiplexer #(.select(1), .width(32), .disabled("Z"), .enable("false")) multiplexer_7 (
    .in0(sqrx_1_c_prime), .in1(sqrx_a_1_c_prime), .out(multiplexer_7_out), .sel(ni_1));
  Multiplexer #(.select(1), .width(32), .disabled("Z"), .enable("false")) multiplexer_8 (
    .in0(sqrx_1_d_prime), .in1(sqrx_a_1_d_prime), .out(multiplexer_8_out), .sel(ni_1));

  // Notes on the sheet:
  //   a
  //   b
  //   c
  //   d
endmodule

module \控制器  (
  input  [5:0] n,
  input  clock,
  input  clear,
  output ni_1,
  output start,
  output clk,
  output clear_2
);

  wire comparator_1_lt, or_1_out, or_2_out;
  wire [7:0] counter_1_q;

  and and_1 (clk, clock, comparator_1_lt);
  Comparator #(.width(8), .mode("twosComplement")) comparator_1 (
    .a(counter_1_q), .b(8'h6), .lt(comparator_1_lt));  // open: gt, eq
  Shift_Register #(.width(1), .length(6), .parallel("true"), .trigger("rising")) shift_register_1 (
    .shift(1'b1), .clk(or_1_out), .out(ni_1), .load(clear), .clr(1'b0), .d0(n[0]), .d1(n[1]), .d2(n[2]),
    .d3(n[3]), .d4(n[4]), .d5(n[5]));  // open: in, q0, q1, q2, q3, q4, q5
  or or_1 (or_1_out, clock, clear);
  Counter #(.width(8), .max('hff), .ongoal("wrap"), .trigger("rising"), .behavior("new")) counter_1 (
    .load(1'b0), .count(1'b1), .Q(counter_1_q), .clk(clk), .clr(clear), .preset(1'b0), .down(1'b0));  // open: D, carry
  or or_2 (or_2_out, start, ni_1);
  D_Flip_Flop #(.trigger("rising"), .Pre_Clr_Positions("ABOVE_BELOW"), .NegatePresetClear("false"), .enable("false"), .NewFFLayout("true")) d_ff_1 (
    .clk(clock), .D(or_2_out), .Q(start), .preset(1'b0), .reset(clear));  // open: Qn

  assign clear_2 = clear;
endmodule

module \斐波那契_Fibonacci_数列计算器验证电路2  (
  input  [5:0] in_1
);

  wire button_1_out, button_2_out, \控制器_1_clear_2 , \控制器_1_clk , \控制器_1_ni_1 , \控制器_1_start ;
  wire [3:0] \fibonacci数显示模块_1_d0 , \fibonacci数显示模块_1_d1 , \fibonacci数显示模块_1_d2 , \fibonacci数显示模块_1_d3 ,
       \fibonacci数显示模块_1_d4 , \fibonacci数显示模块_1_d5 , \fibonacci数显示模块_1_d6 , \fibonacci数显示模块_1_d7 ,
       \fibonacci数显示模块_1_d8 , \fibonacci数显示模块_1_d9 ;
  wire [31:0] \矩阵快速幂算法迭代模块_1_fi ;

  Button button_1 (.out(button_1_out));
  Button button_2 (.out(button_2_out));
  \控制器  \u_控制器_1  (
    .clear(button_1_out), .ni_1(\控制器_1_ni_1 ), .start(\控制器_1_start ), .clk(\控制器_1_clk ),
    .clear_2(\控制器_1_clear_2 ), .n(in_1), .clock(button_2_out));
  \矩阵快速幂算法迭代模块  \u_矩阵快速幂算法迭代模块_1  (
    .Start(\控制器_1_start ), .clk(\控制器_1_clk ), .clr(\控制器_1_clear_2 ), .Fi(\矩阵快速幂算法迭代模块_1_fi ),
    .ni_1(\控制器_1_ni_1 ));
  \Fibonacci数显示模块  \fibonacci数显示模块_1  (
    .in_1(\矩阵快速幂算法迭代模块_1_fi ), .D0(\fibonacci数显示模块_1_d0 ), .D4(\fibonacci数显示模块_1_d4 ),
    .D1(\fibonacci数显示模块_1_d1 ), .D5(\fibonacci数显示模块_1_d5 ), .D2(\fibonacci数显示模块_1_d2 ),
    .D6(\fibonacci数显示模块_1_d6 ), .D3(\fibonacci数显示模块_1_d3 ), .D7(\fibonacci数显示模块_1_d7 ),
    .D8(\fibonacci数显示模块_1_d8 ), .D9(\fibonacci数显示模块_1_d9 ));
  Hex_Digit_Display hex_digit_display_1 (.value(\fibonacci数显示模块_1_d9 ));  // open: dp
  Hex_Digit_Display hex_digit_display_2 (.value(\fibonacci数显示模块_1_d8 ));  // open: dp
  Hex_Digit_Display hex_digit_display_3 (.value(\fibonacci数显示模块_1_d6 ));  // open: dp
  Hex_Digit_Display hex_digit_display_4 (.value(\fibonacci数显示模块_1_d7 ));  // open: dp
  Hex_Digit_Display hex_digit_display_5 (.value(\fibonacci数显示模块_1_d4 ));  // open: dp
  Hex_Digit_Display hex_digit_display_6 (.value(\fibonacci数显示模块_1_d5 ));  // open: dp
  Hex_Digit_Display hex_digit_display_7 (.value(\fibonacci数显示模块_1_d3 ));  // open: dp
  Hex_Digit_Display hex_digit_display_8 (.value(\fibonacci数显示模块_1_d2 ));  // open: dp
  Hex_Digit_Display hex_digit_display_9 (.value(\fibonacci数显示模块_1_d1 ));  // open: dp
  Hex_Digit_Display hex_digit_display_10 (.value(\fibonacci数显示模块_1_d0 ));  // open: dp

  // Notes on the sheet:
  //   使用这一电路有利于观察中间的ni-1和start
endmodule
